// Logisim project grupo40.circ as structural Verilog: 16 circuits, main circuit Main
module Main (
  input  in_1,
  input  in_2,
  input  in_3,
  input  in_4,
  input  in_5,
  input  in_6,
  input  in_7,
  input  in_8
);

  wire button_1_out, button_2_out, button_3_out, button_4_out, movimiento_1_check_pozo, movimiento_1_ganoo,
       movimiento_2_check_pozo, movimiento_2_ganoo, movimiento_4_check_pozo, movimiento_4_ganoo, P1_C0,
       P1_C1, P1_C2, P1_F0, P1_F1, P1_F2, P2_C0, P2_C1, P2_C2, P2_F0, P2_F1, P2_F2, P3_C0, P3_C1, P3_C2,
       P3_F0, P3_F1, P3_F2, P4_C0, P4_C1, P4_C2, P4_F0, P4_F1, P4_F2, rgbled_3_p1, rgbled_3_p2,
       segment7_1_s1, segment7_1_s2, segment7_1_s3, segment7_1_s4, segment7_1_s5, segment7_1_s6,
       segment7_1_s7, segment7_2_s1, segment7_2_s2, segment7_2_s3, segment7_2_s4, segment7_2_s5,
       segment7_2_s6, segment7_2_s7, segment7_3_s1, segment7_3_s2, segment7_3_s3, segment7_3_s4,
       segment7_3_s5, segment7_3_s6, segment7_3_s7, segment7_4_s1, segment7_4_s2, segment7_4_s3,
       segment7_4_s4, segment7_4_s5, segment7_4_s6, segment7_4_s7, segment7_5_s1, segment7_5_s2,
       segment7_5_s3, segment7_5_s4, segment7_5_s5, segment7_5_s6, segment7_5_s7, segment7_6_s1,
       segment7_6_s2, segment7_6_s3, segment7_6_s4, segment7_6_s5, segment7_6_s6, segment7_6_s7,
       segment7_7_s1, segment7_7_s2, segment7_7_s3, segment7_7_s4, segment7_7_s5, segment7_7_s6,
       segment7_7_s7, segment7_8_s1, segment7_8_s2, segment7_8_s3, segment7_8_s4, segment7_8_s5,
       segment7_8_s6, segment7_8_s7;
  wire [1:0] codfilascolumnas_1_f1c1, codfilascolumnas_1_f1c6, codfilascolumnas_1_f2c1,
       codfilascolumnas_1_f2c6, codfilascolumnas_1_f3c1, codfilascolumnas_1_f3c6, codfilascolumnas_1_f4c1,
       codfilascolumnas_1_f4c6, codfilascolumnas_1_f5c1, codfilascolumnas_1_f5c6, codfilascolumnas_1_f6c1,
       codfilascolumnas_1_f6c6, codfilascolumnas_1_out_8, codfilascolumnas_1_out_9,
       codfilascolumnas_1_out_10, codfilascolumnas_1_out_11, codfilascolumnas_1_out_14,
       codfilascolumnas_1_out_15, codfilascolumnas_1_out_16, codfilascolumnas_1_out_17,
       codfilascolumnas_1_out_20, codfilascolumnas_1_out_21, codfilascolumnas_1_out_22,
       codfilascolumnas_1_out_23, codfilascolumnas_1_out_26, codfilascolumnas_1_out_27,
       codfilascolumnas_1_out_28, codfilascolumnas_1_out_29, codfilascolumnas_1_out_32,
       codfilascolumnas_1_out_33, codfilascolumnas_1_out_34, codfilascolumnas_1_out_35,
       codfilascolumnas_1_out_38, codfilascolumnas_1_out_39, codfilascolumnas_1_out_40,
       codfilascolumnas_1_out_41, codfilascolumnas_2_f1c1, codfilascolumnas_2_f1c6, codfilascolumnas_2_f2c1,
       codfilascolumnas_2_f2c6, codfilascolumnas_2_f3c1, codfilascolumnas_2_f3c6, codfilascolumnas_2_f4c1,
       codfilascolumnas_2_f4c6, codfilascolumnas_2_f5c1, codfilascolumnas_2_f5c6, codfilascolumnas_2_f6c1,
       codfilascolumnas_2_f6c6, codfilascolumnas_2_out_8, codfilascolumnas_2_out_9,
       codfilascolumnas_2_out_10, codfilascolumnas_2_out_11, codfilascolumnas_2_out_14,
       codfilascolumnas_2_out_15, codfilascolumnas_2_out_16, codfilascolumnas_2_out_17,
       codfilascolumnas_2_out_20, codfilascolumnas_2_out_21, codfilascolumnas_2_out_22,
       codfilascolumnas_2_out_23, codfilascolumnas_2_out_26, codfilascolumnas_2_out_27,
       codfilascolumnas_2_out_28, codfilascolumnas_2_out_29, codfilascolumnas_2_out_32,
       codfilascolumnas_2_out_33, codfilascolumnas_2_out_34, codfilascolumnas_2_out_35,
       codfilascolumnas_2_out_38, codfilascolumnas_2_out_39, codfilascolumnas_2_out_40,
       codfilascolumnas_2_out_41, codfilascolumnas_3_f1c1, codfilascolumnas_3_f1c6, codfilascolumnas_3_f2c1,
       codfilascolumnas_3_f2c6, codfilascolumnas_3_f3c1, codfilascolumnas_3_f3c6, codfilascolumnas_3_f4c1,
       codfilascolumnas_3_f4c6, codfilascolumnas_3_f5c1, codfilascolumnas_3_f5c6, codfilascolumnas_3_f6c1,
       codfilascolumnas_3_f6c6, codfilascolumnas_3_out_8, codfilascolumnas_3_out_9,
       codfilascolumnas_3_out_10, codfilascolumnas_3_out_11, codfilascolumnas_3_out_14,
       codfilascolumnas_3_out_15, codfilascolumnas_3_out_16, codfilascolumnas_3_out_17,
       codfilascolumnas_3_out_20, codfilascolumnas_3_out_21, codfilascolumnas_3_out_22,
       codfilascolumnas_3_out_23, codfilascolumnas_3_out_26, codfilascolumnas_3_out_27,
       codfilascolumnas_3_out_28, codfilascolumnas_3_out_29, codfilascolumnas_3_out_32,
       codfilascolumnas_3_out_33, codfilascolumnas_3_out_34, codfilascolumnas_3_out_35,
       codfilascolumnas_3_out_38, codfilascolumnas_3_out_39, codfilascolumnas_3_out_40,
       codfilascolumnas_3_out_41, codfilascolumnas_4_f1c1, codfilascolumnas_4_f1c6, codfilascolumnas_4_f2c1,
       codfilascolumnas_4_f2c6, codfilascolumnas_4_f3c1, codfilascolumnas_4_f3c6, codfilascolumnas_4_f4c1,
       codfilascolumnas_4_f4c6, codfilascolumnas_4_f5c1, codfilascolumnas_4_f5c6, codfilascolumnas_4_f6c1,
       codfilascolumnas_4_f6c6, codfilascolumnas_4_out_8, codfilascolumnas_4_out_9,
       codfilascolumnas_4_out_10, codfilascolumnas_4_out_11, codfilascolumnas_4_out_14,
       codfilascolumnas_4_out_15, codfilascolumnas_4_out_16, codfilascolumnas_4_out_17,
       codfilascolumnas_4_out_20, codfilascolumnas_4_out_21, codfilascolumnas_4_out_22,
       codfilascolumnas_4_out_23, codfilascolumnas_4_out_26, codfilascolumnas_4_out_27,
       codfilascolumnas_4_out_28, codfilascolumnas_4_out_29, codfilascolumnas_4_out_32,
       codfilascolumnas_4_out_33, codfilascolumnas_4_out_34, codfilascolumnas_4_out_35,
       codfilascolumnas_4_out_38, codfilascolumnas_4_out_39, codfilascolumnas_4_out_40,
       codfilascolumnas_4_out_41;
  wire [3:0] p1_F1C1, p1_F1C2, p1_F1C3, p1_F1C4, p1_F1C5, p1_F1C6, p1_F2C1, p1_F2C2, p1_F2C3, p1_F2C4,
       p1_F2C5, p1_F2C6, p1_F3C1, p1_F3C2, p1_F3C3, p1_F3C4, p1_F3C5, p1_F3C6, p1_F4C1, p1_F4C2, p1_F4C3,
       p1_F4C4, p1_F4C5, p1_F4C6, p1_F5C1, p1_F5C2, p1_F5C3, p1_F5C4, p1_F5C5, p1_F5C6, p1_F6C1, p1_F6C2,
       p1_F6C3, p1_F6C4, p1_F6C5, p1_F6C6, p2_F1C1, p2_F1C2, p2_F1C3, p2_F1C4, p2_F1C5, p2_F1C6, p2_F2C1,
       p2_F2C2, p2_F2C3, p2_F2C4, p2_F2C5, p2_F2C6, p2_F3C1, p2_F3C2, p2_F3C3, p2_F3C4, p2_F3C5, p2_F3C6,
       p2_F4C1, p2_F4C2, p2_F4C3, p2_F4C4, p2_F4C5, p2_F4C6, p2_F5C1, p2_F5C2, p2_F5C3, p2_F5C4, p2_F5C5,
       p2_F5C6, p2_F6C1, p2_F6C2, p2_F6C3, p2_F6C4, p2_F6C5, p2_F6C6, p3_F1C1, p3_F1C2, p3_F1C3, p3_F1C4,
       p3_F1C5, p3_F1C6, p3_F2C1, p3_F2C2, p3_F2C3, p3_F2C4, p3_F2C5, p3_F2C6, p3_F3C1, p3_F3C2, p3_F3C3,
       p3_F3C4, p3_F3C5, p3_F3C6, p3_F4C1, p3_F4C2, p3_F4C3, p3_F4C4, p3_F4C5, p3_F4C6, p3_F5C1, p3_F5C2,
       p3_F5C3, p3_F5C4, p3_F5C5, p3_F5C6, p3_F6C1, p3_F6C2, p3_F6C3, p3_F6C4, p3_F6C5, p3_F6C6, p4_F1C1,
       p4_F1C2, p4_F1C3, p4_F1C4, p4_F1C5, p4_F1C6, p4_F2C1, p4_F2C2, p4_F2C3, p4_F2C4, p4_F2C5, p4_F2C6,
       p4_F3C1, p4_F3C2, p4_F3C3, p4_F3C4, p4_F3C5, p4_F3C6, p4_F4C1, p4_F4C2, p4_F4C3, p4_F4C4, p4_F4C5,
       p4_F4C6, p4_F5C1, p4_F5C2, p4_F5C3, p4_F5C4, p4_F5C5, p4_F5C6, p4_F6C1, p4_F6C2, p4_F6C3, p4_F6C4,
       p4_F6C5, p4_F6C6;
  wire [7:0] movimiento_1_s0, movimiento_2_s0, movimiento_3_s0, movimiento_4_s0;

  Button button_1 (.out(button_1_out));
  Button button_2 (.out(button_2_out));
  Movimiento movimiento_1 (
    .Boton(button_1_out), .M1(in_3), .M0(in_4), .Ganoo(movimiento_1_ganoo), .S7(movimiento_1_s0[7]),
    .S6(movimiento_1_s0[6]), .S5(movimiento_1_s0[5]), .S4(movimiento_1_s0[4]), .S3(movimiento_1_s0[3]),
    .S2(movimiento_1_s0[2]), .S1(movimiento_1_s0[1]), .S0(movimiento_1_s0[0]),
    .check_pozo(movimiento_1_check_pozo), .F2(P1_F2), .F1(P1_F1), .F0(P1_F0), .C2(P1_C2), .C1(P1_C1),
    .C0(P1_C0));
  Movimiento movimiento_2 (
    .Boton(button_2_out), .M1(in_5), .M0(in_6), .Ganoo(movimiento_2_ganoo), .S7(movimiento_2_s0[7]),
    .S6(movimiento_2_s0[6]), .S5(movimiento_2_s0[5]), .S4(movimiento_2_s0[4]), .S3(movimiento_2_s0[3]),
    .S2(movimiento_2_s0[2]), .S1(movimiento_2_s0[1]), .S0(movimiento_2_s0[0]),
    .check_pozo(movimiento_2_check_pozo), .F2(P3_F2), .F1(P3_F1), .F0(P3_F0), .C2(P3_C2), .C1(P3_C1),
    .C0(P3_C0));
  // RGBLED rgbled_1: pin names not known; wires that end beside it: movimiento_1_ganoo, movimiento_1_check_pozo
  Segment7 segment7_1 (
    .B(P1_C1), .C(P1_C0), .A(P1_C2), .S1(segment7_1_s1), .S4(segment7_1_s4), .S5(segment7_1_s5),
    .S6(segment7_1_s6), .S2(segment7_1_s2), .S7(segment7_1_s7), .S3(segment7_1_s3));
  // RGBLED rgbled_2: pin names not known; wires that end beside it: movimiento_2_ganoo, movimiento_2_check_pozo
  Segment7 segment7_2 (
    .B(P3_C1), .C(P3_C0), .A(P3_C2), .S1(segment7_2_s1), .S4(segment7_2_s4), .S5(segment7_2_s5),
    .S6(segment7_2_s6), .S2(segment7_2_s2), .S7(segment7_2_s7), .S3(segment7_2_s3));
  CodFilasColumnas codfilascolumnas_1 (
    .F2(P1_F2), .F1(P1_F1), .F0(P1_F0), .C2(P1_C2), .C1(P1_C1), .C0(P1_C0), .F1C1(codfilascolumnas_1_f1c1),
    .out_8(codfilascolumnas_1_out_8), .out_9(codfilascolumnas_1_out_9), .out_10(codfilascolumnas_1_out_10),
    .out_11(codfilascolumnas_1_out_11), .F1C6(codfilascolumnas_1_f1c6), .F2C1(codfilascolumnas_1_f2c1),
    .out_14(codfilascolumnas_1_out_14), .out_15(codfilascolumnas_1_out_15),
    .out_16(codfilascolumnas_1_out_16), .out_17(codfilascolumnas_1_out_17), .F2C6(codfilascolumnas_1_f2c6),
    .F3C1(codfilascolumnas_1_f3c1), .out_20(codfilascolumnas_1_out_20), .out_21(codfilascolumnas_1_out_21),
    .out_22(codfilascolumnas_1_out_22), .out_23(codfilascolumnas_1_out_23), .F3C6(codfilascolumnas_1_f3c6),
    .F4C1(codfilascolumnas_1_f4c1), .out_26(codfilascolumnas_1_out_26), .out_27(codfilascolumnas_1_out_27),
    .out_28(codfilascolumnas_1_out_28), .out_29(codfilascolumnas_1_out_29), .F4C6(codfilascolumnas_1_f4c6),
    .F5C1(codfilascolumnas_1_f5c1), .out_32(codfilascolumnas_1_out_32), .out_33(codfilascolumnas_1_out_33),
    .out_34(codfilascolumnas_1_out_34), .out_35(codfilascolumnas_1_out_35), .F5C6(codfilascolumnas_1_f5c6),
    .F6C1(codfilascolumnas_1_f6c1), .out_38(codfilascolumnas_1_out_38), .out_39(codfilascolumnas_1_out_39),
    .out_40(codfilascolumnas_1_out_40), .out_41(codfilascolumnas_1_out_41), .F6C6(codfilascolumnas_1_f6c6));
  _7_Segment_Display u_7_segment_display_1 (.g(movimiento_1_check_pozo));  // open: f, a, b, e, d, c, dp
  _7_Segment_Display u_7_segment_display_2 (
    .g(segment7_1_s1), .f(segment7_1_s2), .a(segment7_1_s3), .b(segment7_1_s4), .e(segment7_1_s5),
    .d(segment7_1_s6), .c(segment7_1_s7));  // open: dp
  _7_Segment_Display u_7_segment_display_3 (.g(movimiento_2_check_pozo));  // open: f, a, b, e, d, c, dp
  _7_Segment_Display u_7_segment_display_4 (
    .g(segment7_2_s1), .f(segment7_2_s2), .a(segment7_2_s3), .b(segment7_2_s4), .e(segment7_2_s5),
    .d(segment7_2_s6), .c(segment7_2_s7));  // open: dp
  assign p1_F1C1 = {{2{codfilascolumnas_1_f1c1[1]}}, codfilascolumnas_1_f1c1};  // Bit_Extender bit_extender_1
  assign p1_F1C2 = {{2{codfilascolumnas_1_out_8[1]}}, codfilascolumnas_1_out_8};  // Bit_Extender bit_extender_2
  assign p1_F1C3 = {{2{codfilascolumnas_1_out_9[1]}}, codfilascolumnas_1_out_9};  // Bit_Extender bit_extender_3
  assign p1_F1C4 = {{2{codfilascolumnas_1_out_10[1]}}, codfilascolumnas_1_out_10};  // Bit_Extender bit_extender_4
  assign p1_F1C5 = {{2{codfilascolumnas_1_out_11[1]}}, codfilascolumnas_1_out_11};  // Bit_Extender bit_extender_5
  assign p1_F1C6 = {{2{codfilascolumnas_1_f1c6[1]}}, codfilascolumnas_1_f1c6};  // Bit_Extender bit_extender_6
  assign p1_F2C1 = {{2{codfilascolumnas_1_f2c1[1]}}, codfilascolumnas_1_f2c1};  // Bit_Extender bit_extender_7
  assign p1_F2C2 = {{2{codfilascolumnas_1_out_14[1]}}, codfilascolumnas_1_out_14};  // Bit_Extender bit_extender_8
  assign p1_F2C3 = {{2{codfilascolumnas_1_out_15[1]}}, codfilascolumnas_1_out_15};  // Bit_Extender bit_extender_9
  assign p1_F2C4 = {{2{codfilascolumnas_1_out_16[1]}}, codfilascolumnas_1_out_16};  // Bit_Extender bit_extender_10
  assign p1_F2C5 = {{2{codfilascolumnas_1_out_17[1]}}, codfilascolumnas_1_out_17};  // Bit_Extender bit_extender_11
  assign p1_F2C6 = {{2{codfilascolumnas_1_f2c6[1]}}, codfilascolumnas_1_f2c6};  // Bit_Extender bit_extender_12
  assign p1_F3C1 = {{2{codfilascolumnas_1_f3c1[1]}}, codfilascolumnas_1_f3c1};  // Bit_Extender bit_extender_13
  assign p1_F3C2 = {{2{codfilascolumnas_1_out_20[1]}}, codfilascolumnas_1_out_20};  // Bit_Extender bit_extender_14
  assign p1_F3C3 = {{2{codfilascolumnas_1_out_21[1]}}, codfilascolumnas_1_out_21};  // Bit_Extender bit_extender_15
  assign p1_F3C4 = {{2{codfilascolumnas_1_out_22[1]}}, codfilascolumnas_1_out_22};  // Bit_Extender bit_extender_16
  assign p1_F3C5 = {{2{codfilascolumnas_1_out_23[1]}}, codfilascolumnas_1_out_23};  // Bit_Extender bit_extender_17
  assign p1_F3C6 = {{2{codfilascolumnas_1_f3c6[1]}}, codfilascolumnas_1_f3c6};  // Bit_Extender bit_extender_18
  assign p1_F4C1 = {{2{codfilascolumnas_1_f4c1[1]}}, codfilascolumnas_1_f4c1};  // Bit_Extender bit_extender_19
  assign p1_F4C2 = {{2{codfilascolumnas_1_out_26[1]}}, codfilascolumnas_1_out_26};  // Bit_Extender bit_extender_20
  assign p1_F4C3 = {{2{codfilascolumnas_1_out_27[1]}}, codfilascolumnas_1_out_27};  // Bit_Extender bit_extender_21
  assign p1_F4C4 = {{2{codfilascolumnas_1_out_28[1]}}, codfilascolumnas_1_out_28};  // Bit_Extender bit_extender_22
  assign p1_F4C5 = {{2{codfilascolumnas_1_out_29[1]}}, codfilascolumnas_1_out_29};  // Bit_Extender bit_extender_23
  assign p1_F4C6 = {{2{codfilascolumnas_1_f4c6[1]}}, codfilascolumnas_1_f4c6};  // Bit_Extender bit_extender_24
  assign p1_F5C1 = {{2{codfilascolumnas_1_f5c1[1]}}, codfilascolumnas_1_f5c1};  // Bit_Extender bit_extender_25
  assign p1_F5C2 = {{2{codfilascolumnas_1_out_32[1]}}, codfilascolumnas_1_out_32};  // Bit_Extender bit_extender_26
  assign p1_F5C3 = {{2{codfilascolumnas_1_out_33[1]}}, codfilascolumnas_1_out_33};  // Bit_Extender bit_extender_27
  assign p1_F5C4 = {{2{codfilascolumnas_1_out_34[1]}}, codfilascolumnas_1_out_34};  // Bit_Extender bit_extender_28
  assign p1_F5C5 = {{2{codfilascolumnas_1_out_35[1]}}, codfilascolumnas_1_out_35};  // Bit_Extender bit_extender_29
  assign p1_F5C6 = {{2{codfilascolumnas_1_f5c6[1]}}, codfilascolumnas_1_f5c6};  // Bit_Extender bit_extender_30
  assign p1_F6C1 = {{2{codfilascolumnas_1_f6c1[1]}}, codfilascolumnas_1_f6c1};  // Bit_Extender bit_extender_31
  assign p1_F6C2 = {{2{codfilascolumnas_1_out_38[1]}}, codfilascolumnas_1_out_38};  // Bit_Extender bit_extender_32
  assign p1_F6C3 = {{2{codfilascolumnas_1_out_39[1]}}, codfilascolumnas_1_out_39};  // Bit_Extender bit_extender_33
  assign p1_F6C4 = {{2{codfilascolumnas_1_out_40[1]}}, codfilascolumnas_1_out_40};  // Bit_Extender bit_extender_34
  assign p1_F6C5 = {{2{codfilascolumnas_1_out_41[1]}}, codfilascolumnas_1_out_41};  // Bit_Extender bit_extender_35
  assign p1_F6C6 = {{2{codfilascolumnas_1_f6c6[1]}}, codfilascolumnas_1_f6c6};  // Bit_Extender bit_extender_36
  _7_Segment_Display u_7_segment_display_5 ();  // open: g, f, a, b, e, d, c, dp
  // BCD_to_7_Segment_decoder bcd_to_7_segment_decoder_1: pin names not known
  // Binary_to_BCD_converter #(.binvalue(8)) binary_to_bcd_converter_1: pin names not known; wires that end beside it: movimiento_1_s0
  Segment7 segment7_3 (
    .B(P1_F1), .C(P1_F0), .A(P1_F2), .S1(segment7_3_s1), .S4(segment7_3_s4), .S5(segment7_3_s5),
    .S6(segment7_3_s6), .S2(segment7_3_s2), .S7(segment7_3_s7), .S3(segment7_3_s3));
  _7_Segment_Display u_7_segment_display_6 ();  // open: g, f, a, b, e, d, c, dp
  // BCD_to_7_Segment_decoder bcd_to_7_segment_decoder_2: pin names not known
  // Binary_to_BCD_converter #(.binvalue(8)) binary_to_bcd_converter_2: pin names not known; wires that end beside it: movimiento_2_s0
  Segment7 segment7_4 (
    .B(P3_F1), .C(P3_F0), .A(P3_F2), .S1(segment7_4_s1), .S4(segment7_4_s4), .S5(segment7_4_s5),
    .S6(segment7_4_s6), .S2(segment7_4_s2), .S7(segment7_4_s7), .S3(segment7_4_s3));
  _7_Segment_Display u_7_segment_display_7 ();  // open: g, f, a, b, e, d, c, dp
  // BCD_to_7_Segment_decoder bcd_to_7_segment_decoder_3: pin names not known
  _7_Segment_Display u_7_segment_display_8 (
    .g(segment7_3_s1), .f(segment7_3_s2), .a(segment7_3_s3), .b(segment7_3_s4), .e(segment7_3_s5),
    .d(segment7_3_s6), .c(segment7_3_s7));  // open: dp
  _7_Segment_Display u_7_segment_display_9 ();  // open: g, f, a, b, e, d, c, dp
  _7_Segment_Display u_7_segment_display_10 ();  // open: g, f, a, b, e, d, c, dp
  // BCD_to_7_Segment_decoder bcd_to_7_segment_decoder_4: pin names not known
  // BCD_to_7_Segment_decoder bcd_to_7_segment_decoder_5: pin names not known
  _7_Segment_Display u_7_segment_display_11 (
    .g(segment7_4_s1), .f(segment7_4_s2), .a(segment7_4_s3), .b(segment7_4_s4), .e(segment7_4_s5),
    .d(segment7_4_s6), .c(segment7_4_s7));  // open: dp
  _7_Segment_Display u_7_segment_display_12 ();  // open: g, f, a, b, e, d, c, dp
  // BCD_to_7_Segment_decoder bcd_to_7_segment_decoder_6: pin names not known
  DotMatrix #(.matrixcols(4), .matrixrows(4)) dotmatrix_1 (
    .col0(p1_F1C1), .col1(p1_F1C1), .col2(p1_F1C1), .col3(p1_F1C1));
  DotMatrix #(.matrixcols(4), .matrixrows(4)) dotmatrix_2 (
    .col0(p2_F1C1), .col1(p2_F1C1), .col2(p2_F1C1), .col3(p2_F1C1));
  DotMatrix #(.matrixcols(4), .matrixrows(4)) dotmatrix_3 (
    .col0(p3_F1C1), .col1(p3_F1C1), .col2(p3_F1C1), .col3(p3_F1C1));
  DotMatrix #(.matrixcols(4), .matrixrows(4)) dotmatrix_4 (
    .col0(p4_F1C1), .col1(p4_F1C1), .col2(p4_F1C1), .col3(p4_F1C1));
  DotMatrix #(.matrixcols(4), .matrixrows(4)) dotmatrix_5 (
    .col0(p1_F2C1), .col1(p1_F2C1), .col2(p1_F2C1), .col3(p1_F2C1));
  DotMatrix #(.matrixcols(4), .matrixrows(4)) dotmatrix_6 (
    .col0(p2_F2C1), .col1(p2_F2C1), .col2(p2_F2C1), .col3(p2_F2C1));
  DotMatrix #(.matrixcols(4), .matrixrows(4)) dotmatrix_7 (
    .col0(p3_F2C1), .col1(p3_F2C1), .col2(p3_F2C1), .col3(p3_F2C1));
  DotMatrix #(.matrixcols(4), .matrixrows(4)) dotmatrix_8 (
    .col0(p4_F2C1), .col1(p4_F2C1), .col2(p4_F2C1), .col3(p4_F2C1));
  DotMatrix #(.matrixcols(4), .matrixrows(4)) dotmatrix_9 (
    .col0(p1_F3C1), .col1(p1_F3C1), .col2(p1_F3C1), .col3(p1_F3C1));
  DotMatrix #(.matrixcols(4), .matrixrows(4)) dotmatrix_10 (
    .col0(p2_F3C1), .col1(p2_F3C1), .col2(p2_F3C1), .col3(p2_F3C1));
  DotMatrix #(.matrixcols(4), .matrixrows(4)) dotmatrix_11 (
    .col0(p3_F3C1), .col1(p3_F3C1), .col2(p3_F3C1), .col3(p3_F3C1));
  DotMatrix #(.matrixcols(4), .matrixrows(4)) dotmatrix_12 (
    .col0(p4_F3C1), .col1(p4_F3C1), .col2(p4_F3C1), .col3(p4_F3C1));
  DotMatrix #(.matrixcols(4), .matrixrows(4)) dotmatrix_13 (
    .col0(p1_F4C1), .col1(p1_F4C1), .col2(p1_F4C1), .col3(p1_F4C1));
  DotMatrix #(.matrixcols(4), .matrixrows(4)) dotmatrix_14 (
    .col0(p2_F4C1), .col1(p2_F4C1), .col2(p2_F4C1), .col3(p2_F4C1));
  DotMatrix #(.matrixcols(4), .matrixrows(4)) dotmatrix_15 (
    .col0(p3_F4C1), .col1(p3_F4C1), .col2(p3_F4C1), .col3(p3_F4C1));
  DotMatrix #(.matrixcols(4), .matrixrows(4)) dotmatrix_16 (
    .col0(p4_F4C1), .col1(p4_F4C1), .col2(p4_F4C1), .col3(p4_F4C1));
  DotMatrix #(.matrixcols(4), .matrixrows(4)) dotmatrix_17 (
    .col0(p1_F5C1), .col1(p1_F5C1), .col2(p1_F5C1), .col3(p1_F5C1));
  DotMatrix #(.matrixcols(4), .matrixrows(4)) dotmatrix_18 (
    .col0(p2_F5C1), .col1(p2_F5C1), .col2(p2_F5C1), .col3(p2_F5C1));
  DotMatrix #(.matrixcols(4), .matrixrows(4)) dotmatrix_19 (
    .col0(p3_F5C1), .col1(p3_F5C1), .col2(p3_F5C1), .col3(p3_F5C1));
  DotMatrix #(.matrixcols(4), .matrixrows(4)) dotmatrix_20 (
    .col0(p4_F5C1), .col1(p4_F5C1), .col2(p4_F5C1), .col3(p4_F5C1));
  DotMatrix #(.matrixcols(4), .matrixrows(4)) dotmatrix_21 (
    .col0(p1_F6C1), .col1(p1_F6C1), .col2(p1_F6C1), .col3(p1_F6C1));
  DotMatrix #(.matrixcols(4), .matrixrows(4)) dotmatrix_22 (
    .col0(p2_F6C1), .col1(p2_F6C1), .col2(p2_F6C1), .col3(p2_F6C1));
  DotMatrix #(.matrixcols(4), .matrixrows(4)) dotmatrix_23 (
    .col0(p3_F6C1), .col1(p3_F6C1), .col2(p3_F6C1), .col3(p3_F6C1));
  DotMatrix #(.matrixcols(4), .matrixrows(4)) dotmatrix_24 (
    .col0(p4_F6C1), .col1(p4_F6C1), .col2(p4_F6C1), .col3(p4_F6C1));
  DotMatrix #(.matrixcols(4), .matrixrows(4)) dotmatrix_25 (
    .col0(p1_F1C2), .col1(p1_F1C2), .col2(p1_F1C2), .col3(p1_F1C2));
  DotMatrix #(.matrixcols(4), .matrixrows(4)) dotmatrix_26 (
    .col0(p3_F1C2), .col1(p3_F1C2), .col2(p3_F1C2), .col3(p3_F1C2));
  DotMatrix #(.matrixcols(4), .matrixrows(4)) dotmatrix_27 (
    .col0(p1_F2C2), .col1(p1_F2C2), .col2(p1_F2C2), .col3(p1_F2C2));
  DotMatrix #(.matrixcols(4), .matrixrows(4)) dotmatrix_28 (
    .col0(p3_F2C2), .col1(p3_F2C2), .col2(p3_F2C2), .col3(p3_F2C2));
  DotMatrix #(.matrixcols(4), .matrixrows(4)) dotmatrix_29 (
    .col0(p1_F3C2), .col1(p1_F3C2), .col2(p1_F3C2), .col3(p1_F3C2));
  DotMatrix #(.matrixcols(4), .matrixrows(4)) dotmatrix_30 (
    .col0(p3_F3C2), .col1(p3_F3C2), .col2(p3_F3C2), .col3(p3_F3C2));
  DotMatrix #(.matrixcols(4), .matrixrows(4)) dotmatrix_31 (
    .col0(p1_F4C2), .col1(p1_F4C2), .col2(p1_F4C2), .col3(p1_F4C2));
  DotMatrix #(.matrixcols(4), .matrixrows(4)) dotmatrix_32 (
    .col0(p3_F4C2), .col1(p3_F4C2), .col2(p3_F4C2), .col3(p3_F4C2));
  DotMatrix #(.matrixcols(4), .matrixrows(4)) dotmatrix_33 (
    .col0(p1_F5C2), .col1(p1_F5C2), .col2(p1_F5C2), .col3(p1_F5C2));
  DotMatrix #(.matrixcols(4), .matrixrows(4)) dotmatrix_34 (
    .col0(p3_F5C2), .col1(p3_F5C2), .col2(p3_F5C2), .col3(p3_F5C2));
  DotMatrix #(.matrixcols(4), .matrixrows(4)) dotmatrix_35 (
    .col0(p1_F6C2), .col1(p1_F6C2), .col2(p1_F6C2), .col3(p1_F6C2));
  DotMatrix #(.matrixcols(4), .matrixrows(4)) dotmatrix_36 (
    .col0(p3_F6C2), .col1(p3_F6C2), .col2(p3_F6C2), .col3(p3_F6C2));
  Clock clock_1 ();  // open: out
  DotMatrix #(.matrixcols(4), .matrixrows(4)) dotmatrix_37 (
    .col0(p1_F1C3), .col1(p1_F1C3), .col2(p1_F1C3), .col3(p1_F1C3));
  DotMatrix #(.matrixcols(4), .matrixrows(4)) dotmatrix_38 (
    .col0(p2_F1C2), .col1(p2_F1C2), .col2(p2_F1C2), .col3(p2_F1C2));
  DotMatrix #(.matrixcols(4), .matrixrows(4)) dotmatrix_39 (
    .col0(p3_F1C3), .col1(p3_F1C3), .col2(p3_F1C3), .col3(p3_F1C3));
  DotMatrix #(.matrixcols(4), .matrixrows(4)) dotmatrix_40 (
    .col0(p4_F1C2), .col1(p4_F1C2), .col2(p4_F1C2), .col3(p4_F1C2));
  DotMatrix #(.matrixcols(4), .matrixrows(4)) dotmatrix_41 (
    .col0(p1_F2C3), .col1(p1_F2C3), .col2(p1_F2C3), .col3(p1_F2C3));
  DotMatrix #(.matrixcols(4), .matrixrows(4)) dotmatrix_42 (
    .col0(p2_F2C2), .col1(p2_F2C2), .col2(p2_F2C2), .col3(p2_F2C2));
  DotMatrix #(.matrixcols(4), .matrixrows(4)) dotmatrix_43 (
    .col0(p3_F2C3), .col1(p3_F2C3), .col2(p3_F2C3), .col3(p3_F2C3));
  DotMatrix #(.matrixcols(4), .matrixrows(4)) dotmatrix_44 (
    .col0(p4_F2C2), .col1(p4_F2C2), .col2(p4_F2C2), .col3(p4_F2C2));
  DotMatrix #(.matrixcols(4), .matrixrows(4)) dotmatrix_45 (
    .col0(p1_F3C3), .col1(p1_F3C3), .col2(p1_F3C3), .col3(p1_F3C3));
  DotMatrix #(.matrixcols(4), .matrixrows(4)) dotmatrix_46 (
    .col0(p2_F3C2), .col1(p2_F3C2), .col2(p2_F3C2), .col3(p2_F3C2));
  DotMatrix #(.matrixcols(4), .matrixrows(4)) dotmatrix_47 (
    .col0(p3_F3C3), .col1(p3_F3C3), .col2(p3_F3C3), .col3(p3_F3C3));
  DotMatrix #(.matrixcols(4), .matrixrows(4)) dotmatrix_48 (
    .col0(p4_F3C2), .col1(p4_F3C2), .col2(p4_F3C2), .col3(p4_F3C2));
  DotMatrix #(.matrixcols(4), .matrixrows(4)) dotmatrix_49 (
    .col0(p1_F4C3), .col1(p1_F4C3), .col2(p1_F4C3), .col3(p1_F4C3));
  DotMatrix #(.matrixcols(4), .matrixrows(4)) dotmatrix_50 (
    .col0(p2_F4C2), .col1(p2_F4C2), .col2(p2_F4C2), .col3(p2_F4C2));
  DotMatrix #(.matrixcols(4), .matrixrows(4)) dotmatrix_51 (
    .col0(p3_F4C3), .col1(p3_F4C3), .col2(p3_F4C3), .col3(p3_F4C3));
  DotMatrix #(.matrixcols(4), .matrixrows(4)) dotmatrix_52 (
    .col0(p4_F4C2), .col1(p4_F4C2), .col2(p4_F4C2), .col3(p4_F4C2));
  DotMatrix #(.matrixcols(4), .matrixrows(4)) dotmatrix_53 (
    .col0(p1_F5C3), .col1(p1_F5C3), .col2(p1_F5C3), .col3(p1_F5C3));
  DotMatrix #(.matrixcols(4), .matrixrows(4)) dotmatrix_54 (
    .col0(p2_F5C2), .col1(p2_F5C2), .col2(p2_F5C2), .col3(p2_F5C2));
  DotMatrix #(.matrixcols(4), .matrixrows(4)) dotmatrix_55 (
    .col0(p3_F5C3), .col1(p3_F5C3), .col2(p3_F5C3), .col3(p3_F5C3));
  DotMatrix #(.matrixcols(4), .matrixrows(4)) dotmatrix_56 (
    .col0(p4_F5C2), .col1(p4_F5C2), .col2(p4_F5C2), .col3(p4_F5C2));
  DotMatrix #(.matrixcols(4), .matrixrows(4)) dotmatrix_57 (
    .col0(p1_F6C3), .col1(p1_F6C3), .col2(p1_F6C3), .col3(p1_F6C3));
  DotMatrix #(.matrixcols(4), .matrixrows(4)) dotmatrix_58 (
    .col0(p2_F6C2), .col1(p2_F6C2), .col2(p2_F6C2), .col3(p2_F6C2));
  DotMatrix #(.matrixcols(4), .matrixrows(4)) dotmatrix_59 (
    .col0(p3_F6C3), .col1(p3_F6C3), .col2(p3_F6C3), .col3(p3_F6C3));
  DotMatrix #(.matrixcols(4), .matrixrows(4)) dotmatrix_60 (
    .col0(p4_F6C2), .col1(p4_F6C2), .col2(p4_F6C2), .col3(p4_F6C2));
  CodFilasColumnas codfilascolumnas_2 (
    .F2(P2_F2), .F1(P2_F1), .F0(P2_F0), .C2(P2_C2), .C1(P2_C1), .C0(P2_C0), .F1C1(codfilascolumnas_2_f1c1),
    .out_8(codfilascolumnas_2_out_8), .out_9(codfilascolumnas_2_out_9), .out_10(codfilascolumnas_2_out_10),
    .out_11(codfilascolumnas_2_out_11), .F1C6(codfilascolumnas_2_f1c6), .F2C1(codfilascolumnas_2_f2c1),
    .out_14(codfilascolumnas_2_out_14), .out_15(codfilascolumnas_2_out_15),
    .out_16(codfilascolumnas_2_out_16), .out_17(codfilascolumnas_2_out_17), .F2C6(codfilascolumnas_2_f2c6),
    .F3C1(codfilascolumnas_2_f3c1), .out_20(codfilascolumnas_2_out_20), .out_21(codfilascolumnas_2_out_21),
    .out_22(codfilascolumnas_2_out_22), .out_23(codfilascolumnas_2_out_23), .F3C6(codfilascolumnas_2_f3c6),
    .F4C1(codfilascolumnas_2_f4c1), .out_26(codfilascolumnas_2_out_26), .out_27(codfilascolumnas_2_out_27),
    .out_28(codfilascolumnas_2_out_28), .out_29(codfilascolumnas_2_out_29), .F4C6(codfilascolumnas_2_f4c6),
    .F5C1(codfilascolumnas_2_f5c1), .out_32(codfilascolumnas_2_out_32), .out_33(codfilascolumnas_2_out_33),
    .out_34(codfilascolumnas_2_out_34), .out_35(codfilascolumnas_2_out_35), .F5C6(codfilascolumnas_2_f5c6),
    .F6C1(codfilascolumnas_2_f6c1), .out_38(codfilascolumnas_2_out_38), .out_39(codfilascolumnas_2_out_39),
    .out_40(codfilascolumnas_2_out_40), .out_41(codfilascolumnas_2_out_41), .F6C6(codfilascolumnas_2_f6c6));
  DotMatrix #(.matrixcols(4), .matrixrows(4)) dotmatrix_61 (
    .col0(p2_F1C3), .col1(p2_F1C3), .col2(p2_F1C3), .col3(p2_F1C3));
  DotMatrix #(.matrixcols(4), .matrixrows(4)) dotmatrix_62 (
    .col0(p1_F1C4), .col1(p1_F1C4), .col2(p1_F1C4), .col3(p1_F1C4));
  DotMatrix #(.matrixcols(4), .matrixrows(4)) dotmatrix_63 (
    .col0(p4_F1C3), .col1(p4_F1C3), .col2(p4_F1C3), .col3(p4_F1C3));
  DotMatrix #(.matrixcols(4), .matrixrows(4)) dotmatrix_64 (
    .col0(p3_F1C4), .col1(p3_F1C4), .col2(p3_F1C4), .col3(p3_F1C4));
  DotMatrix #(.matrixcols(4), .matrixrows(4)) dotmatrix_65 (
    .col0(p2_F2C3), .col1(p2_F2C3), .col2(p2_F2C3), .col3(p2_F2C3));
  DotMatrix #(.matrixcols(4), .matrixrows(4)) dotmatrix_66 (
    .col0(p1_F2C4), .col1(p1_F2C4), .col2(p1_F2C4), .col3(p1_F2C4));
  DotMatrix #(.matrixcols(4), .matrixrows(4)) dotmatrix_67 (
    .col0(p4_F2C3), .col1(p4_F2C3), .col2(p4_F2C3), .col3(p4_F2C3));
  DotMatrix #(.matrixcols(4), .matrixrows(4)) dotmatrix_68 (
    .col0(p3_F2C4), .col1(p3_F2C4), .col2(p3_F2C4), .col3(p3_F2C4));
  DotMatrix #(.matrixcols(4), .matrixrows(4)) dotmatrix_69 (
    .col0(p2_F3C3), .col1(p2_F3C3), .col2(p2_F3C3), .col3(p2_F3C3));
  DotMatrix #(.matrixcols(4), .matrixrows(4)) dotmatrix_70 (
    .col0(p1_F3C4), .col1(p1_F3C4), .col2(p1_F3C4), .col3(p1_F3C4));
  DotMatrix #(.matrixcols(4), .matrixrows(4)) dotmatrix_71 (
    .col0(p4_F3C3), .col1(p4_F3C3), .col2(p4_F3C3), .col3(p4_F3C3));
  DotMatrix #(.matrixcols(4), .matrixrows(4)) dotmatrix_72 (
    .col0(p3_F3C4), .col1(p3_F3C4), .col2(p3_F3C4), .col3(p3_F3C4));
  DotMatrix #(.matrixcols(4), .matrixrows(4)) dotmatrix_73 (
    .col0(p2_F4C3), .col1(p2_F4C3), .col2(p2_F4C3), .col3(p2_F4C3));
  DotMatrix #(.matrixcols(4), .matrixrows(4)) dotmatrix_74 (
    .col0(p1_F4C4), .col1(p1_F4C4), .col2(p1_F4C4), .col3(p1_F4C4));
  DotMatrix #(.matrixcols(4), .matrixrows(4)) dotmatrix_75 (
    .col0(p4_F4C3), .col1(p4_F4C3), .col2(p4_F4C3), .col3(p4_F4C3));
  DotMatrix #(.matrixcols(4), .matrixrows(4)) dotmatrix_76 (
    .col0(p3_F4C4), .col1(p3_F4C4), .col2(p3_F4C4), .col3(p3_F4C4));
  DotMatrix #(.matrixcols(4), .matrixrows(4)) dotmatrix_77 (
    .col0(p2_F5C3), .col1(p2_F5C3), .col2(p2_F5C3), .col3(p2_F5C3));
  DotMatrix #(.matrixcols(4), .matrixrows(4)) dotmatrix_78 (
    .col0(p1_F5C4), .col1(p1_F5C4), .col2(p1_F5C4), .col3(p1_F5C4));
  DotMatrix #(.matrixcols(4), .matrixrows(4)) dotmatrix_79 (
    .col0(p4_F5C3), .col1(p4_F5C3), .col2(p4_F5C3), .col3(p4_F5C3));
  DotMatrix #(.matrixcols(4), .matrixrows(4)) dotmatrix_80 (
    .col0(p3_F5C4), .col1(p3_F5C4), .col2(p3_F5C4), .col3(p3_F5C4));
  DotMatrix #(.matrixcols(4), .matrixrows(4)) dotmatrix_81 (
    .col0(p2_F6C3), .col1(p2_F6C3), .col2(p2_F6C3), .col3(p2_F6C3));
  DotMatrix #(.matrixcols(4), .matrixrows(4)) dotmatrix_82 (
    .col0(p1_F6C4), .col1(p1_F6C4), .col2(p1_F6C4), .col3(p1_F6C4));
  DotMatrix #(.matrixcols(4), .matrixrows(4)) dotmatrix_83 (
    .col0(p4_F6C3), .col1(p4_F6C3), .col2(p4_F6C3), .col3(p4_F6C3));
  DotMatrix #(.matrixcols(4), .matrixrows(4)) dotmatrix_84 (
    .col0(p3_F6C4), .col1(p3_F6C4), .col2(p3_F6C4), .col3(p3_F6C4));
  assign p2_F1C1 = {{2{codfilascolumnas_2_f1c1[1]}}, codfilascolumnas_2_f1c1};  // Bit_Extender bit_extender_37
  assign p2_F1C2 = {{2{codfilascolumnas_2_out_8[1]}}, codfilascolumnas_2_out_8};  // Bit_Extender bit_extender_38
  assign p2_F1C3 = {{2{codfilascolumnas_2_out_9[1]}}, codfilascolumnas_2_out_9};  // Bit_Extender bit_extender_39
  assign p2_F1C4 = {{2{codfilascolumnas_2_out_10[1]}}, codfilascolumnas_2_out_10};  // Bit_Extender bit_extender_40
  assign p2_F1C5 = {{2{codfilascolumnas_2_out_11[1]}}, codfilascolumnas_2_out_11};  // Bit_Extender bit_extender_41
  assign p2_F1C6 = {{2{codfilascolumnas_2_f1c6[1]}}, codfilascolumnas_2_f1c6};  // Bit_Extender bit_extender_42
  assign p2_F2C1 = {{2{codfilascolumnas_2_f2c1[1]}}, codfilascolumnas_2_f2c1};  // Bit_Extender bit_extender_43
  assign p2_F2C2 = {{2{codfilascolumnas_2_out_14[1]}}, codfilascolumnas_2_out_14};  // Bit_Extender bit_extender_44
  assign p2_F2C3 = {{2{codfilascolumnas_2_out_15[1]}}, codfilascolumnas_2_out_15};  // Bit_Extender bit_extender_45
  assign p2_F2C4 = {{2{codfilascolumnas_2_out_16[1]}}, codfilascolumnas_2_out_16};  // Bit_Extender bit_extender_46
  assign p2_F2C5 = {{2{codfilascolumnas_2_out_17[1]}}, codfilascolumnas_2_out_17};  // Bit_Extender bit_extender_47
  assign p2_F2C6 = {{2{codfilascolumnas_2_f2c6[1]}}, codfilascolumnas_2_f2c6};  // Bit_Extender bit_extender_48
  assign p2_F3C1 = {{2{codfilascolumnas_2_f3c1[1]}}, codfilascolumnas_2_f3c1};  // Bit_Extender bit_extender_49
  assign p2_F3C2 = {{2{codfilascolumnas_2_out_20[1]}}, codfilascolumnas_2_out_20};  // Bit_Extender bit_extender_50
  assign p2_F3C3 = {{2{codfilascolumnas_2_out_21[1]}}, codfilascolumnas_2_out_21};  // Bit_Extender bit_extender_51
  assign p2_F3C4 = {{2{codfilascolumnas_2_out_22[1]}}, codfilascolumnas_2_out_22};  // Bit_Extender bit_extender_52
  assign p2_F3C5 = {{2{codfilascolumnas_2_out_23[1]}}, codfilascolumnas_2_out_23};  // Bit_Extender bit_extender_53
  assign p2_F3C6 = {{2{codfilascolumnas_2_f3c6[1]}}, codfilascolumnas_2_f3c6};  // Bit_Extender bit_extender_54
  assign p2_F4C1 = {{2{codfilascolumnas_2_f4c1[1]}}, codfilascolumnas_2_f4c1};  // Bit_Extender bit_extender_55
  assign p2_F4C2 = {{2{codfilascolumnas_2_out_26[1]}}, codfilascolumnas_2_out_26};  // Bit_Extender bit_extender_56
  assign p2_F4C3 = {{2{codfilascolumnas_2_out_27[1]}}, codfilascolumnas_2_out_27};  // Bit_Extender bit_extender_57
  assign p2_F4C4 = {{2{codfilascolumnas_2_out_28[1]}}, codfilascolumnas_2_out_28};  // Bit_Extender bit_extender_58
  assign p2_F4C5 = {{2{codfilascolumnas_2_out_29[1]}}, codfilascolumnas_2_out_29};  // Bit_Extender bit_extender_59
  assign p2_F4C6 = {{2{codfilascolumnas_2_f4c6[1]}}, codfilascolumnas_2_f4c6};  // Bit_Extender bit_extender_60
  assign p2_F5C1 = {{2{codfilascolumnas_2_f5c1[1]}}, codfilascolumnas_2_f5c1};  // Bit_Extender bit_extender_61
  assign p2_F5C2 = {{2{codfilascolumnas_2_out_32[1]}}, codfilascolumnas_2_out_32};  // Bit_Extender bit_extender_62
  assign p2_F5C3 = {{2{codfilascolumnas_2_out_33[1]}}, codfilascolumnas_2_out_33};  // Bit_Extender bit_extender_63
  assign p2_F5C4 = {{2{codfilascolumnas_2_out_34[1]}}, codfilascolumnas_2_out_34};  // Bit_Extender bit_extender_64
  assign p2_F5C5 = {{2{codfilascolumnas_2_out_35[1]}}, codfilascolumnas_2_out_35};  // Bit_Extender bit_extender_65
  assign p2_F5C6 = {{2{codfilascolumnas_2_f5c6[1]}}, codfilascolumnas_2_f5c6};  // Bit_Extender bit_extender_66
  assign p2_F6C1 = {{2{codfilascolumnas_2_f6c1[1]}}, codfilascolumnas_2_f6c1};  // Bit_Extender bit_extender_67
  assign p2_F6C2 = {{2{codfilascolumnas_2_out_38[1]}}, codfilascolumnas_2_out_38};  // Bit_Extender bit_extender_68
  assign p2_F6C3 = {{2{codfilascolumnas_2_out_39[1]}}, codfilascolumnas_2_out_39};  // Bit_Extender bit_extender_69
  assign p2_F6C4 = {{2{codfilascolumnas_2_out_40[1]}}, codfilascolumnas_2_out_40};  // Bit_Extender bit_extender_70
  assign p2_F6C5 = {{2{codfilascolumnas_2_out_41[1]}}, codfilascolumnas_2_out_41};  // Bit_Extender bit_extender_71
  assign p2_F6C6 = {{2{codfilascolumnas_2_f6c6[1]}}, codfilascolumnas_2_f6c6};  // Bit_Extender bit_extender_72
  DotMatrix #(.matrixcols(4), .matrixrows(4)) dotmatrix_85 (
    .col0(p2_F1C4), .col1(p2_F1C4), .col2(p2_F1C4), .col3(p2_F1C4));
  DotMatrix #(.matrixcols(4), .matrixrows(4)) dotmatrix_86 (
    .col0(p1_F1C5), .col1(p1_F1C5), .col2(p1_F1C5), .col3(p1_F1C5));
  DotMatrix #(.matrixcols(4), .matrixrows(4)) dotmatrix_87 (
    .col0(p4_F1C4), .col1(p4_F1C4), .col2(p4_F1C4), .col3(p4_F1C4));
  DotMatrix #(.matrixcols(4), .matrixrows(4)) dotmatrix_88 (
    .col0(p3_F1C5), .col1(p3_F1C5), .col2(p3_F1C5), .col3(p3_F1C5));
  DotMatrix #(.matrixcols(4), .matrixrows(4)) dotmatrix_89 (
    .col0(p2_F2C4), .col1(p2_F2C4), .col2(p2_F2C4), .col3(p2_F2C4));
  DotMatrix #(.matrixcols(4), .matrixrows(4)) dotmatrix_90 (
    .col0(p1_F2C5), .col1(p1_F2C5), .col2(p1_F2C5), .col3(p1_F2C5));
  DotMatrix #(.matrixcols(4), .matrixrows(4)) dotmatrix_91 (
    .col0(p4_F2C4), .col1(p4_F2C4), .col2(p4_F2C4), .col3(p4_F2C4));
  DotMatrix #(.matrixcols(4), .matrixrows(4)) dotmatrix_92 (
    .col0(p3_F2C5), .col1(p3_F2C5), .col2(p3_F2C5), .col3(p3_F2C5));
  DotMatrix #(.matrixcols(4), .matrixrows(4)) dotmatrix_93 (
    .col0(p2_F3C4), .col1(p2_F3C4), .col2(p2_F3C4), .col3(p2_F3C4));
  DotMatrix #(.matrixcols(4), .matrixrows(4)) dotmatrix_94 (
    .col0(p1_F3C5), .col1(p1_F3C5), .col2(p1_F3C5), .col3(p1_F3C5));
  DotMatrix #(.matrixcols(4), .matrixrows(4)) dotmatrix_95 (
    .col0(p4_F3C4), .col1(p4_F3C4), .col2(p4_F3C4), .col3(p4_F3C4));
  DotMatrix #(.matrixcols(4), .matrixrows(4)) dotmatrix_96 (
    .col0(p3_F3C5), .col1(p3_F3C5), .col2(p3_F3C5), .col3(p3_F3C5));
  DotMatrix #(.matrixcols(4), .matrixrows(4)) dotmatrix_97 (
    .col0(p2_F4C4), .col1(p2_F4C4), .col2(p2_F4C4), .col3(p2_F4C4));
  DotMatrix #(.matrixcols(4), .matrixrows(4)) dotmatrix_98 (
    .col0(p1_F4C5), .col1(p1_F4C5), .col2(p1_F4C5), .col3(p1_F4C5));
  DotMatrix #(.matrixcols(4), .matrixrows(4)) dotmatrix_99 (
    .col0(p4_F4C4), .col1(p4_F4C4), .col2(p4_F4C4), .col3(p4_F4C4));
  DotMatrix #(.matrixcols(4), .matrixrows(4)) dotmatrix_100 (
    .col0(p3_F4C5), .col1(p3_F4C5), .col2(p3_F4C5), .col3(p3_F4C5));
  DotMatrix #(.matrixcols(4), .matrixrows(4)) dotmatrix_101 (
    .col0(p2_F5C4), .col1(p2_F5C4), .col2(p2_F5C4), .col3(p2_F5C4));
  DotMatrix #(.matrixcols(4), .matrixrows(4)) dotmatrix_102 (
    .col0(p1_F5C5), .col1(p1_F5C5), .col2(p1_F5C5), .col3(p1_F5C5));
  DotMatrix #(.matrixcols(4), .matrixrows(4)) dotmatrix_103 (
    .col0(p4_F5C4), .col1(p4_F5C4), .col2(p4_F5C4), .col3(p4_F5C4));
  DotMatrix #(.matrixcols(4), .matrixrows(4)) dotmatrix_104 (
    .col0(p3_F5C5), .col1(p3_F5C5), .col2(p3_F5C5), .col3(p3_F5C5));
  DotMatrix #(.matrixcols(4), .matrixrows(4)) dotmatrix_105 (
    .col0(p2_F6C4), .col1(p2_F6C4), .col2(p2_F6C4), .col3(p2_F6C4));
  DotMatrix #(.matrixcols(4), .matrixrows(4)) dotmatrix_106 (
    .col0(p1_F6C5), .col1(p1_F6C5), .col2(p1_F6C5), .col3(p1_F6C5));
  DotMatrix #(.matrixcols(4), .matrixrows(4)) dotmatrix_107 (
    .col0(p4_F6C4), .col1(p4_F6C4), .col2(p4_F6C4), .col3(p4_F6C4));
  DotMatrix #(.matrixcols(4), .matrixrows(4)) dotmatrix_108 (
    .col0(p3_F6C5), .col1(p3_F6C5), .col2(p3_F6C5), .col3(p3_F6C5));
  DotMatrix #(.matrixcols(4), .matrixrows(4)) dotmatrix_109 (
    .col0(p2_F1C5), .col1(p2_F1C5), .col2(p2_F1C5), .col3(p2_F1C5));
  DotMatrix #(.matrixcols(4), .matrixrows(4)) dotmatrix_110 (
    .col0(p4_F1C5), .col1(p4_F1C5), .col2(p4_F1C5), .col3(p4_F1C5));
  DotMatrix #(.matrixcols(4), .matrixrows(4)) dotmatrix_111 (
    .col0(p2_F2C5), .col1(p2_F2C5), .col2(p2_F2C5), .col3(p2_F2C5));
  DotMatrix #(.matrixcols(4), .matrixrows(4)) dotmatrix_112 (
    .col0(p4_F2C5), .col1(p4_F2C5), .col2(p4_F2C5), .col3(p4_F2C5));
  DotMatrix #(.matrixcols(4), .matrixrows(4)) dotmatrix_113 (
    .col0(p2_F3C5), .col1(p2_F3C5), .col2(p2_F3C5), .col3(p2_F3C5));
  DotMatrix #(.matrixcols(4), .matrixrows(4)) dotmatrix_114 (
    .col0(p4_F3C5), .col1(p4_F3C5), .col2(p4_F3C5), .col3(p4_F3C5));
  DotMatrix #(.matrixcols(4), .matrixrows(4)) dotmatrix_115 (
    .col0(p2_F4C5), .col1(p2_F4C5), .col2(p2_F4C5), .col3(p2_F4C5));
  DotMatrix #(.matrixcols(4), .matrixrows(4)) dotmatrix_116 (
    .col0(p4_F4C5), .col1(p4_F4C5), .col2(p4_F4C5), .col3(p4_F4C5));
  DotMatrix #(.matrixcols(4), .matrixrows(4)) dotmatrix_117 (
    .col0(p2_F5C5), .col1(p2_F5C5), .col2(p2_F5C5), .col3(p2_F5C5));
  DotMatrix #(.matrixcols(4), .matrixrows(4)) dotmatrix_118 (
    .col0(p4_F5C5), .col1(p4_F5C5), .col2(p4_F5C5), .col3(p4_F5C5));
  DotMatrix #(.matrixcols(4), .matrixrows(4)) dotmatrix_119 (
    .col0(p2_F6C5), .col1(p2_F6C5), .col2(p2_F6C5), .col3(p2_F6C5));
  DotMatrix #(.matrixcols(4), .matrixrows(4)) dotmatrix_120 (
    .col0(p4_F6C5), .col1(p4_F6C5), .col2(p4_F6C5), .col3(p4_F6C5));
  DotMatrix #(.matrixcols(4), .matrixrows(4)) dotmatrix_121 (
    .col0(p1_F1C6), .col1(p1_F1C6), .col2(p1_F1C6), .col3(p1_F1C6));
  DotMatrix #(.matrixcols(4), .matrixrows(4)) dotmatrix_122 (
    .col0(p2_F1C6), .col1(p2_F1C6), .col2(p2_F1C6), .col3(p2_F1C6));
  DotMatrix #(.matrixcols(4), .matrixrows(4)) dotmatrix_123 (
    .col0(p3_F1C6), .col1(p3_F1C6), .col2(p3_F1C6), .col3(p3_F1C6));
  DotMatrix #(.matrixcols(4), .matrixrows(4)) dotmatrix_124 (
    .col0(p4_F1C6), .col1(p4_F1C6), .col2(p4_F1C6), .col3(p4_F1C6));
  DotMatrix #(.matrixcols(4), .matrixrows(4)) dotmatrix_125 (
    .col0(p1_F2C6), .col1(p1_F2C6), .col2(p1_F2C6), .col3(p1_F2C6));
  DotMatrix #(.matrixcols(4), .matrixrows(4)) dotmatrix_126 (
    .col0(p2_F2C6), .col1(p2_F2C6), .col2(p2_F2C6), .col3(p2_F2C6));
  DotMatrix #(.matrixcols(4), .matrixrows(4)) dotmatrix_127 (
    .col0(p3_F2C6), .col1(p3_F2C6), .col2(p3_F2C6), .col3(p3_F2C6));
  DotMatrix #(.matrixcols(4), .matrixrows(4)) dotmatrix_128 (
    .col0(p4_F2C6), .col1(p4_F2C6), .col2(p4_F2C6), .col3(p4_F2C6));
  DotMatrix #(.matrixcols(4), .matrixrows(4)) dotmatrix_129 (
    .col0(p1_F3C6), .col1(p1_F3C6), .col2(p1_F3C6), .col3(p1_F3C6));
  DotMatrix #(.matrixcols(4), .matrixrows(4)) dotmatrix_130 (
    .col0(p2_F3C6), .col1(p2_F3C6), .col2(p2_F3C6), .col3(p2_F3C6));
  DotMatrix #(.matrixcols(4), .matrixrows(4)) dotmatrix_131 (
    .col0(p3_F3C6), .col1(p3_F3C6), .col2(p3_F3C6), .col3(p3_F3C6));
  DotMatrix #(.matrixcols(4), .matrixrows(4)) dotmatrix_132 (
    .col0(p4_F3C6), .col1(p4_F3C6), .col2(p4_F3C6), .col3(p4_F3C6));
  DotMatrix #(.matrixcols(4), .matrixrows(4)) dotmatrix_133 (
    .col0(p1_F4C6), .col1(p1_F4C6), .col2(p1_F4C6), .col3(p1_F4C6));
  DotMatrix #(.matrixcols(4), .matrixrows(4)) dotmatrix_134 (
    .col0(p2_F4C6), .col1(p2_F4C6), .col2(p2_F4C6), .col3(p2_F4C6));
  DotMatrix #(.matrixcols(4), .matrixrows(4)) dotmatrix_135 (
    .col0(p3_F4C6), .col1(p3_F4C6), .col2(p3_F4C6), .col3(p3_F4C6));
  DotMatrix #(.matrixcols(4), .matrixrows(4)) dotmatrix_136 (
    .col0(p4_F4C6), .col1(p4_F4C6), .col2(p4_F4C6), .col3(p4_F4C6));
  DotMatrix #(.matrixcols(4), .matrixrows(4)) dotmatrix_137 (
    .col0(p1_F5C6), .col1(p1_F5C6), .col2(p1_F5C6), .col3(p1_F5C6));
  DotMatrix #(.matrixcols(4), .matrixrows(4)) dotmatrix_138 (
    .col0(p2_F5C6), .col1(p2_F5C6), .col2(p2_F5C6), .col3(p2_F5C6));
  DotMatrix #(.matrixcols(4), .matrixrows(4)) dotmatrix_139 (
    .col0(p3_F5C6), .col1(p3_F5C6), .col2(p3_F5C6), .col3(p3_F5C6));
  DotMatrix #(.matrixcols(4), .matrixrows(4)) dotmatrix_140 (
    .col0(p4_F5C6), .col1(p4_F5C6), .col2(p4_F5C6), .col3(p4_F5C6));
  DotMatrix #(.matrixcols(4), .matrixrows(4)) dotmatrix_141 (
    .col0(p1_F6C6), .col1(p1_F6C6), .col2(p1_F6C6), .col3(p1_F6C6));
  DotMatrix #(.matrixcols(4), .matrixrows(4)) dotmatrix_142 (
    .col0(p2_F6C6), .col1(p2_F6C6), .col2(p2_F6C6), .col3(p2_F6C6));
  DotMatrix #(.matrixcols(4), .matrixrows(4)) dotmatrix_143 (
    .col0(p3_F6C6), .col1(p3_F6C6), .col2(p3_F6C6), .col3(p3_F6C6));
  DotMatrix #(.matrixcols(4), .matrixrows(4)) dotmatrix_144 (
    .col0(p4_F6C6), .col1(p4_F6C6), .col2(p4_F6C6), .col3(p4_F6C6));
  Button button_3 (.out(button_3_out));
  Button button_4 (.out(button_4_out));
  CodFilasColumnas codfilascolumnas_3 (
    .F2(P4_F2), .F1(P4_F1), .F0(P4_F0), .C2(P4_C2), .C1(P4_C1), .C0(P4_C0), .F1C1(codfilascolumnas_3_f1c1),
    .out_8(codfilascolumnas_3_out_8), .out_9(codfilascolumnas_3_out_9), .out_10(codfilascolumnas_3_out_10),
    .out_11(codfilascolumnas_3_out_11), .F1C6(codfilascolumnas_3_f1c6), .F2C1(codfilascolumnas_3_f2c1),
    .out_14(codfilascolumnas_3_out_14), .out_15(codfilascolumnas_3_out_15),
    .out_16(codfilascolumnas_3_out_16), .out_17(codfilascolumnas_3_out_17), .F2C6(codfilascolumnas_3_f2c6),
    .F3C1(codfilascolumnas_3_f3c1), .out_20(codfilascolumnas_3_out_20), .out_21(codfilascolumnas_3_out_21),
    .out_22(codfilascolumnas_3_out_22), .out_23(codfilascolumnas_3_out_23), .F3C6(codfilascolumnas_3_f3c6),
    .F4C1(codfilascolumnas_3_f4c1), .out_26(codfilascolumnas_3_out_26), .out_27(codfilascolumnas_3_out_27),
    .out_28(codfilascolumnas_3_out_28), .out_29(codfilascolumnas_3_out_29), .F4C6(codfilascolumnas_3_f4c6),
    .F5C1(codfilascolumnas_3_f5c1), .out_32(codfilascolumnas_3_out_32), .out_33(codfilascolumnas_3_out_33),
    .out_34(codfilascolumnas_3_out_34), .out_35(codfilascolumnas_3_out_35), .F5C6(codfilascolumnas_3_f5c6),
    .F6C1(codfilascolumnas_3_f6c1), .out_38(codfilascolumnas_3_out_38), .out_39(codfilascolumnas_3_out_39),
    .out_40(codfilascolumnas_3_out_40), .out_41(codfilascolumnas_3_out_41), .F6C6(codfilascolumnas_3_f6c6));
  assign p4_F1C1 = {{2{codfilascolumnas_3_f1c1[1]}}, codfilascolumnas_3_f1c1};  // Bit_Extender bit_extender_73
  assign p4_F1C2 = {{2{codfilascolumnas_3_out_8[1]}}, codfilascolumnas_3_out_8};  // Bit_Extender bit_extender_74
  assign p4_F1C3 = {{2{codfilascolumnas_3_out_9[1]}}, codfilascolumnas_3_out_9};  // Bit_Extender bit_extender_75
  assign p4_F1C4 = {{2{codfilascolumnas_3_out_10[1]}}, codfilascolumnas_3_out_10};  // Bit_Extender bit_extender_76
  assign p4_F1C5 = {{2{codfilascolumnas_3_out_11[1]}}, codfilascolumnas_3_out_11};  // Bit_Extender bit_extender_77
  assign p4_F1C6 = {{2{codfilascolumnas_3_f1c6[1]}}, codfilascolumnas_3_f1c6};  // Bit_Extender bit_extender_78
  assign p4_F2C1 = {{2{codfilascolumnas_3_f2c1[1]}}, codfilascolumnas_3_f2c1};  // Bit_Extender bit_extender_79
  assign p4_F2C2 = {{2{codfilascolumnas_3_out_14[1]}}, codfilascolumnas_3_out_14};  // Bit_Extender bit_extender_80
  assign p4_F2C3 = {{2{codfilascolumnas_3_out_15[1]}}, codfilascolumnas_3_out_15};  // Bit_Extender bit_extender_81
  assign p4_F2C4 = {{2{codfilascolumnas_3_out_16[1]}}, codfilascolumnas_3_out_16};  // Bit_Extender bit_extender_82
  assign p4_F2C5 = {{2{codfilascolumnas_3_out_17[1]}}, codfilascolumnas_3_out_17};  // Bit_Extender bit_extender_83
  assign p4_F2C6 = {{2{codfilascolumnas_3_f2c6[1]}}, codfilascolumnas_3_f2c6};  // Bit_Extender bit_extender_84
  assign p4_F3C1 = {{2{codfilascolumnas_3_f3c1[1]}}, codfilascolumnas_3_f3c1};  // Bit_Extender bit_extender_85
  assign p4_F3C2 = {{2{codfilascolumnas_3_out_20[1]}}, codfilascolumnas_3_out_20};  // Bit_Extender bit_extender_86
  assign p4_F3C3 = {{2{codfilascolumnas_3_out_21[1]}}, codfilascolumnas_3_out_21};  // Bit_Extender bit_extender_87
  assign p4_F3C4 = {{2{codfilascolumnas_3_out_22[1]}}, codfilascolumnas_3_out_22};  // Bit_Extender bit_extender_88
  assign p4_F3C5 = {{2{codfilascolumnas_3_out_23[1]}}, codfilascolumnas_3_out_23};  // Bit_Extender bit_extender_89
  assign p4_F3C6 = {{2{codfilascolumnas_3_f3c6[1]}}, codfilascolumnas_3_f3c6};  // Bit_Extender bit_extender_90
  assign p4_F4C1 = {{2{codfilascolumnas_3_f4c1[1]}}, codfilascolumnas_3_f4c1};  // Bit_Extender bit_extender_91
  assign p4_F4C2 = {{2{codfilascolumnas_3_out_26[1]}}, codfilascolumnas_3_out_26};  // Bit_Extender bit_extender_92
  assign p4_F4C3 = {{2{codfilascolumnas_3_out_27[1]}}, codfilascolumnas_3_out_27};  // Bit_Extender bit_extender_93
  assign p4_F4C4 = {{2{codfilascolumnas_3_out_28[1]}}, codfilascolumnas_3_out_28};  // Bit_Extender bit_extender_94
  assign p4_F4C5 = {{2{codfilascolumnas_3_out_29[1]}}, codfilascolumnas_3_out_29};  // Bit_Extender bit_extender_95
  assign p4_F4C6 = {{2{codfilascolumnas_3_f4c6[1]}}, codfilascolumnas_3_f4c6};  // Bit_Extender bit_extender_96
  assign p4_F5C1 = {{2{codfilascolumnas_3_f5c1[1]}}, codfilascolumnas_3_f5c1};  // Bit_Extender bit_extender_97
  assign p4_F5C2 = {{2{codfilascolumnas_3_out_32[1]}}, codfilascolumnas_3_out_32};  // Bit_Extender bit_extender_98
  assign p4_F5C3 = {{2{codfilascolumnas_3_out_33[1]}}, codfilascolumnas_3_out_33};  // Bit_Extender bit_extender_99
  assign p4_F5C4 = {{2{codfilascolumnas_3_out_34[1]}}, codfilascolumnas_3_out_34};  // Bit_Extender bit_extender_100
  assign p4_F5C5 = {{2{codfilascolumnas_3_out_35[1]}}, codfilascolumnas_3_out_35};  // Bit_Extender bit_extender_101
  assign p4_F5C6 = {{2{codfilascolumnas_3_f5c6[1]}}, codfilascolumnas_3_f5c6};  // Bit_Extender bit_extender_102
  assign p4_F6C1 = {{2{codfilascolumnas_3_f6c1[1]}}, codfilascolumnas_3_f6c1};  // Bit_Extender bit_extender_103
  assign p4_F6C2 = {{2{codfilascolumnas_3_out_38[1]}}, codfilascolumnas_3_out_38};  // Bit_Extender bit_extender_104
  assign p4_F6C3 = {{2{codfilascolumnas_3_out_39[1]}}, codfilascolumnas_3_out_39};  // Bit_Extender bit_extender_105
  assign p4_F6C4 = {{2{codfilascolumnas_3_out_40[1]}}, codfilascolumnas_3_out_40};  // Bit_Extender bit_extender_106
  assign p4_F6C5 = {{2{codfilascolumnas_3_out_41[1]}}, codfilascolumnas_3_out_41};  // Bit_Extender bit_extender_107
  assign p4_F6C6 = {{2{codfilascolumnas_3_f6c6[1]}}, codfilascolumnas_3_f6c6};  // Bit_Extender bit_extender_108
  // RGBLED rgbled_3: pin names not known; wires that end beside it: rgbled_3_p1, rgbled_3_p2
  Movimiento movimiento_3 (
    .Boton(button_3_out), .M1(in_1), .M0(in_2), .Ganoo(rgbled_3_p1), .S7(movimiento_3_s0[7]),
    .S6(movimiento_3_s0[6]), .S5(movimiento_3_s0[5]), .S4(movimiento_3_s0[4]), .S3(movimiento_3_s0[3]),
    .S2(movimiento_3_s0[2]), .S1(movimiento_3_s0[1]), .S0(movimiento_3_s0[0]), .check_pozo(rgbled_3_p2),
    .F2(P2_F2), .F1(P2_F1), .F0(P2_F0), .C2(P2_C2), .C1(P2_C1), .C0(P2_C0));
  Movimiento movimiento_4 (
    .Boton(button_4_out), .M1(in_7), .M0(in_8), .Ganoo(movimiento_4_ganoo), .S7(movimiento_4_s0[7]),
    .S6(movimiento_4_s0[6]), .S5(movimiento_4_s0[5]), .S4(movimiento_4_s0[4]), .S3(movimiento_4_s0[3]),
    .S2(movimiento_4_s0[2]), .S1(movimiento_4_s0[1]), .S0(movimiento_4_s0[0]),
    .check_pozo(movimiento_4_check_pozo), .F2(P4_F2), .F1(P4_F1), .F0(P4_F0), .C2(P4_C2), .C1(P4_C1),
    .C0(P4_C0));
  Segment7 segment7_5 (
    .B(P2_C1), .C(P2_C0), .A(P2_C2), .S1(segment7_5_s1), .S4(segment7_5_s4), .S5(segment7_5_s5),
    .S6(segment7_5_s6), .S2(segment7_5_s2), .S7(segment7_5_s7), .S3(segment7_5_s3));
  _7_Segment_Display u_7_segment_display_13 (
    .g(segment7_5_s1), .f(segment7_5_s2), .a(segment7_5_s3), .b(segment7_5_s4), .e(segment7_5_s5),
    .d(segment7_5_s6), .c(segment7_5_s7));  // open: dp
  // RGBLED rgbled_4: pin names not known; wires that end beside it: movimiento_4_ganoo, movimiento_4_check_pozo
  Segment7 segment7_6 (
    .B(P4_C1), .C(P4_C0), .A(P4_C2), .S1(segment7_6_s1), .S4(segment7_6_s4), .S5(segment7_6_s5),
    .S6(segment7_6_s6), .S2(segment7_6_s2), .S7(segment7_6_s7), .S3(segment7_6_s3));
  _7_Segment_Display u_7_segment_display_14 (.g(rgbled_3_p2));  // open: f, a, b, e, d, c, dp
  _7_Segment_Display u_7_segment_display_15 (.g(movimiento_4_check_pozo));  // open: f, a, b, e, d, c, dp
  _7_Segment_Display u_7_segment_display_16 (
    .g(segment7_6_s1), .f(segment7_6_s2), .a(segment7_6_s3), .b(segment7_6_s4), .e(segment7_6_s5),
    .d(segment7_6_s6), .c(segment7_6_s7));  // open: dp
  _7_Segment_Display u_7_segment_display_17 ();  // open: g, f, a, b, e, d, c, dp
  _7_Segment_Display u_7_segment_display_18 ();  // open: g, f, a, b, e, d, c, dp
  // BCD_to_7_Segment_decoder bcd_to_7_segment_decoder_7: pin names not known
  // BCD_to_7_Segment_decoder bcd_to_7_segment_decoder_8: pin names not known
  // Binary_to_BCD_converter #(.binvalue(8)) binary_to_bcd_converter_3: pin names not known; wires that end beside it: movimiento_3_s0
  Segment7 segment7_7 (
    .B(P2_F1), .C(P2_F0), .A(P2_F2), .S1(segment7_7_s1), .S4(segment7_7_s4), .S5(segment7_7_s5),
    .S6(segment7_7_s6), .S2(segment7_7_s2), .S7(segment7_7_s7), .S3(segment7_7_s3));
  _7_Segment_Display u_7_segment_display_19 (
    .g(segment7_7_s1), .f(segment7_7_s2), .a(segment7_7_s3), .b(segment7_7_s4), .e(segment7_7_s5),
    .d(segment7_7_s6), .c(segment7_7_s7));  // open: dp
  _7_Segment_Display u_7_segment_display_20 ();  // open: g, f, a, b, e, d, c, dp
  // BCD_to_7_Segment_decoder bcd_to_7_segment_decoder_9: pin names not known
  // Binary_to_BCD_converter #(.binvalue(8)) binary_to_bcd_converter_4: pin names not known; wires that end beside it: movimiento_4_s0
  Segment7 segment7_8 (
    .B(P4_F1), .C(P4_F0), .A(P4_F2), .S1(segment7_8_s1), .S4(segment7_8_s4), .S5(segment7_8_s5),
    .S6(segment7_8_s6), .S2(segment7_8_s2), .S7(segment7_8_s7), .S3(segment7_8_s3));
  _7_Segment_Display u_7_segment_display_21 ();  // open: g, f, a, b, e, d, c, dp
  // BCD_to_7_Segment_decoder bcd_to_7_segment_decoder_10: pin names not known
  _7_Segment_Display u_7_segment_display_22 ();  // open: g, f, a, b, e, d, c, dp
  _7_Segment_Display u_7_segment_display_23 ();  // open: g, f, a, b, e, d, c, dp
  // BCD_to_7_Segment_decoder bcd_to_7_segment_decoder_11: pin names not known
  // BCD_to_7_Segment_decoder bcd_to_7_segment_decoder_12: pin names not known
  _7_Segment_Display u_7_segment_display_24 (
    .g(segment7_8_s1), .f(segment7_8_s2), .a(segment7_8_s3), .b(segment7_8_s4), .e(segment7_8_s5),
    .d(segment7_8_s6), .c(segment7_8_s7));  // open: dp
  CodFilasColumnas codfilascolumnas_4 (
    .F2(P3_F2), .F1(P3_F1), .F0(P3_F0), .C2(P3_C2), .C1(P3_C1), .C0(P3_C0), .F1C1(codfilascolumnas_4_f1c1),
    .out_8(codfilascolumnas_4_out_8), .out_9(codfilascolumnas_4_out_9), .out_10(codfilascolumnas_4_out_10),
    .out_11(codfilascolumnas_4_out_11), .F1C6(codfilascolumnas_4_f1c6), .F2C1(codfilascolumnas_4_f2c1),
    .out_14(codfilascolumnas_4_out_14), .out_15(codfilascolumnas_4_out_15),
    .out_16(codfilascolumnas_4_out_16), .out_17(codfilascolumnas_4_out_17), .F2C6(codfilascolumnas_4_f2c6),
    .F3C1(codfilascolumnas_4_f3c1), .out_20(codfilascolumnas_4_out_20), .out_21(codfilascolumnas_4_out_21),
    .out_22(codfilascolumnas_4_out_22), .out_23(codfilascolumnas_4_out_23), .F3C6(codfilascolumnas_4_f3c6),
    .F4C1(codfilascolumnas_4_f4c1), .out_26(codfilascolumnas_4_out_26), .out_27(codfilascolumnas_4_out_27),
    .out_28(codfilascolumnas_4_out_28), .out_29(codfilascolumnas_4_out_29), .F4C6(codfilascolumnas_4_f4c6),
    .F5C1(codfilascolumnas_4_f5c1), .out_32(codfilascolumnas_4_out_32), .out_33(codfilascolumnas_4_out_33),
    .out_34(codfilascolumnas_4_out_34), .out_35(codfilascolumnas_4_out_35), .F5C6(codfilascolumnas_4_f5c6),
    .F6C1(codfilascolumnas_4_f6c1), .out_38(codfilascolumnas_4_out_38), .out_39(codfilascolumnas_4_out_39),
    .out_40(codfilascolumnas_4_out_40), .out_41(codfilascolumnas_4_out_41), .F6C6(codfilascolumnas_4_f6c6));
  assign p3_F1C1 = {{2{codfilascolumnas_4_f1c1[1]}}, codfilascolumnas_4_f1c1};  // Bit_Extender bit_extender_109
  assign p3_F1C2 = {{2{codfilascolumnas_4_out_8[1]}}, codfilascolumnas_4_out_8};  // Bit_Extender bit_extender_110
  assign p3_F1C3 = {{2{codfilascolumnas_4_out_9[1]}}, codfilascolumnas_4_out_9};  // Bit_Extender bit_extender_111
  assign p3_F1C4 = {{2{codfilascolumnas_4_out_10[1]}}, codfilascolumnas_4_out_10};  // Bit_Extender bit_extender_112
  assign p3_F1C5 = {{2{codfilascolumnas_4_out_11[1]}}, codfilascolumnas_4_out_11};  // Bit_Extender bit_extender_113
  assign p3_F1C6 = {{2{codfilascolumnas_4_f1c6[1]}}, codfilascolumnas_4_f1c6};  // Bit_Extender bit_extender_114
  assign p3_F2C1 = {{2{codfilascolumnas_4_f2c1[1]}}, codfilascolumnas_4_f2c1};  // Bit_Extender bit_extender_115
  assign p3_F2C2 = {{2{codfilascolumnas_4_out_14[1]}}, codfilascolumnas_4_out_14};  // Bit_Extender bit_extender_116
  assign p3_F2C3 = {{2{codfilascolumnas_4_out_15[1]}}, codfilascolumnas_4_out_15};  // Bit_Extender bit_extender_117
  assign p3_F2C4 = {{2{codfilascolumnas_4_out_16[1]}}, codfilascolumnas_4_out_16};  // Bit_Extender bit_extender_118
  assign p3_F2C5 = {{2{codfilascolumnas_4_out_17[1]}}, codfilascolumnas_4_out_17};  // Bit_Extender bit_extender_119
  assign p3_F2C6 = {{2{codfilascolumnas_4_f2c6[1]}}, codfilascolumnas_4_f2c6};  // Bit_Extender bit_extender_120
  assign p3_F3C1 = {{2{codfilascolumnas_4_f3c1[1]}}, codfilascolumnas_4_f3c1};  // Bit_Extender bit_extender_121
  assign p3_F3C2 = {{2{codfilascolumnas_4_out_20[1]}}, codfilascolumnas_4_out_20};  // Bit_Extender bit_extender_122
  assign p3_F3C3 = {{2{codfilascolumnas_4_out_21[1]}}, codfilascolumnas_4_out_21};  // Bit_Extender bit_extender_123
  assign p3_F3C4 = {{2{codfilascolumnas_4_out_22[1]}}, codfilascolumnas_4_out_22};  // Bit_Extender bit_extender_124
  assign p3_F3C5 = {{2{codfilascolumnas_4_out_23[1]}}, codfilascolumnas_4_out_23};  // Bit_Extender bit_extender_125
  assign p3_F3C6 = {{2{codfilascolumnas_4_f3c6[1]}}, codfilascolumnas_4_f3c6};  // Bit_Extender bit_extender_126
  assign p3_F4C1 = {{2{codfilascolumnas_4_f4c1[1]}}, codfilascolumnas_4_f4c1};  // Bit_Extender bit_extender_127
  assign p3_F4C2 = {{2{codfilascolumnas_4_out_26[1]}}, codfilascolumnas_4_out_26};  // Bit_Extender bit_extender_128
  assign p3_F4C3 = {{2{codfilascolumnas_4_out_27[1]}}, codfilascolumnas_4_out_27};  // Bit_Extender bit_extender_129
  assign p3_F4C4 = {{2{codfilascolumnas_4_out_28[1]}}, codfilascolumnas_4_out_28};  // Bit_Extender bit_extender_130
  assign p3_F4C5 = {{2{codfilascolumnas_4_out_29[1]}}, codfilascolumnas_4_out_29};  // Bit_Extender bit_extender_131
  assign p3_F4C6 = {{2{codfilascolumnas_4_f4c6[1]}}, codfilascolumnas_4_f4c6};  // Bit_Extender bit_extender_132
  assign p3_F5C1 = {{2{codfilascolumnas_4_f5c1[1]}}, codfilascolumnas_4_f5c1};  // Bit_Extender bit_extender_133
  assign p3_F5C2 = {{2{codfilascolumnas_4_out_32[1]}}, codfilascolumnas_4_out_32};  // Bit_Extender bit_extender_134
  assign p3_F5C3 = {{2{codfilascolumnas_4_out_33[1]}}, codfilascolumnas_4_out_33};  // Bit_Extender bit_extender_135
  assign p3_F5C4 = {{2{codfilascolumnas_4_out_34[1]}}, codfilascolumnas_4_out_34};  // Bit_Extender bit_extender_136
  assign p3_F5C5 = {{2{codfilascolumnas_4_out_35[1]}}, codfilascolumnas_4_out_35};  // Bit_Extender bit_extender_137
  assign p3_F5C6 = {{2{codfilascolumnas_4_f5c6[1]}}, codfilascolumnas_4_f5c6};  // Bit_Extender bit_extender_138
  assign p3_F6C1 = {{2{codfilascolumnas_4_f6c1[1]}}, codfilascolumnas_4_f6c1};  // Bit_Extender bit_extender_139
  assign p3_F6C2 = {{2{codfilascolumnas_4_out_38[1]}}, codfilascolumnas_4_out_38};  // Bit_Extender bit_extender_140
  assign p3_F6C3 = {{2{codfilascolumnas_4_out_39[1]}}, codfilascolumnas_4_out_39};  // Bit_Extender bit_extender_141
  assign p3_F6C4 = {{2{codfilascolumnas_4_out_40[1]}}, codfilascolumnas_4_out_40};  // Bit_Extender bit_extender_142
  assign p3_F6C5 = {{2{codfilascolumnas_4_out_41[1]}}, codfilascolumnas_4_out_41};  // Bit_Extender bit_extender_143
  assign p3_F6C6 = {{2{codfilascolumnas_4_f6c6[1]}}, codfilascolumnas_4_f6c6};  // Bit_Extender bit_extender_144

  // Notes on the sheet:
  //   JUGADOR 1
  //   00 = Abajo
  //   10 = Arriba
  //   01 = Derecha
  //   11 = Izquierda
  //   JUGADOR 3
  //   00 = Abajo
  //   10 = Arriba
  //   01 = Derecha
  //   11 = Izquierda
  //   GANO O PERDIO?
  //   GANO O PERDIO?
  //   Columna (eje X) 
  //   Columna (eje X) 
  //   Puntos
  //   Puntos
  //   Fila (eje Y)
  //   Fila (eje Y)
  //   Para comenzar: Ctrl+K
  //   Frecuencia 8 Hz
  //   JUGADOR  2
  //   00 = Abajo
  //   10 = Arriba
  //   01 = Derecha
  //   11 = Izquierda
  //   JUGADOR 4
  //   00 = Abajo
  //   10 = Arriba
  //   01 = Derecha
  //   11 = Izquierda
  //   GANO O PERDIO?
  //   Columna (eje X) 
  //   GANO O PERDIO?
  //   Columna (eje X) 
  //   Puntos
  //   Fila (eje Y)
  //   Puntos
  //   Fila (eje Y)
endmodule

module CodFilasColumnas (
  input  F2,
  input  F1,
  input  F0,
  input  C2,
  input  C1,
  input  C0,
  output [1:0] F1C1,
  output [1:0] out_8,
  output [1:0] out_9,
  output [1:0] out_10,
  output [1:0] out_11,
  output [1:0] F1C6,
  output [1:0] F2C1,
  output [1:0] out_14,
  output [1:0] out_15,
  output [1:0] out_16,
  output [1:0] out_17,
  output [1:0] F2C6,
  output [1:0] F3C1,
  output [1:0] out_20,
  output [1:0] out_21,
  output [1:0] out_22,
  output [1:0] out_23,
  output [1:0] F3C6,
  output [1:0] F4C1,
  output [1:0] out_26,
  output [1:0] out_27,
  output [1:0] out_28,
  output [1:0] out_29,
  output [1:0] F4C6,
  output [1:0] F5C1,
  output [1:0] out_32,
  output [1:0] out_33,
  output [1:0] out_34,
  output [1:0] out_35,
  output [1:0] F5C6,
  output [1:0] F6C1,
  output [1:0] out_38,
  output [1:0] out_39,
  output [1:0] out_40,
  output [1:0] out_41,
  output [1:0] F6C6
);

  wire and_1_out, and_2_out, and_3_out, and_4_out, and_5_out, and_6_out, and_7_out, and_8_out, and_9_out,
       and_10_out, and_11_out, and_12_out;

  and and_1 (and_1_out, ~F2, ~F1, ~F0);  // AND_Gate
  and and_2 (and_2_out, ~F2, ~F1, F0);  // AND_Gate
  and and_3 (and_3_out, ~F2, F1, ~F0);  // AND_Gate
  and and_4 (and_4_out, ~F2, F1, F0);  // AND_Gate
  and and_5 (and_5_out, F2, ~F1, ~F0);  // AND_Gate
  and and_6 (and_6_out, F2, ~F1, F0);  // AND_Gate
  and and_7 (and_7_out, ~C2, ~C1, ~C0);  // AND_Gate
  and and_8 (and_8_out, ~C2, ~C1, C0);  // AND_Gate
  and and_9 (and_9_out, ~C2, C1, ~C0);  // AND_Gate
  and and_10 (and_10_out, ~C2, C1, C0);  // AND_Gate
  and and_11 (and_11_out, C2, ~C1, ~C0);  // AND_Gate
  and and_12 (and_12_out, C2, ~C1, C0);  // AND_Gate
  CodMatriz codmatriz_1 (
    .C1(and_7_out), .C2(and_8_out), .C3(and_9_out), .C4(and_10_out), .C5(and_11_out), .C6(and_12_out),
    .F1(and_1_out), .F2(and_2_out), .F3(and_3_out), .F4(and_4_out), .F5(and_5_out), .F6(and_6_out),
    .F1C1(F1C1[1]), .F1C2(out_8[1]), .F1C3(out_9[1]), .F1C4(out_10[1]), .F1C5(out_11[1]), .F1C6(F1C6[1]),
    .F2C1(F2C1[1]), .F2C2(out_14[1]), .F2C3(out_15[1]), .F2C4(out_16[1]), .F2C5(out_17[1]), .F2C6(F2C6[1]),
    .F3C1(F3C1[1]), .F3C2(out_20[1]), .F3C3(out_21[1]), .F3C4(out_22[1]), .F3C5(out_23[1]), .F3C6(F3C6[1]),
    .F4C1(F4C1[1]), .F4C2(out_26[1]), .F4C3(out_27[1]), .F4C4(out_28[1]), .F4C5(out_29[1]), .F4C6(F4C6[1]),
    .F5C1(F5C1[1]), .F5C2(out_32[1]), .F5C3(out_33[1]), .F5C4(out_34[1]), .F5C5(out_35[1]), .F5C6(F5C6[1]),
    .F6C1(F6C1[1]), .F6C2(out_38[1]), .F6C3(out_39[1]), .F6C4(out_40[1]), .F6C5(out_41[1]), .F6C6(F6C6[1]));

  assign F1C1[0] = F1C1[1];
  assign F1C6[0] = F1C6[1];
  assign F2C1[0] = F2C1[1];
  assign F2C6[0] = F2C6[1];
  assign F3C1[0] = F3C1[1];
  assign F3C6[0] = F3C6[1];
  assign F4C1[0] = F4C1[1];
  assign F4C6[0] = F4C6[1];
  assign F5C1[0] = F5C1[1];
  assign F5C6[0] = F5C6[1];
  assign F6C1[0] = F6C1[1];
  assign F6C6[0] = F6C6[1];
  assign out_8[0] = out_8[1];
  assign out_9[0] = out_9[1];
  assign out_10[0] = out_10[1];
  assign out_11[0] = out_11[1];
  assign out_14[0] = out_14[1];
  assign out_15[0] = out_15[1];
  assign out_16[0] = out_16[1];
  assign out_17[0] = out_17[1];
  assign out_20[0] = out_20[1];
  assign out_21[0] = out_21[1];
  assign out_22[0] = out_22[1];
  assign out_23[0] = out_23[1];
  assign out_26[0] = out_26[1];
  assign out_27[0] = out_27[1];
  assign out_28[0] = out_28[1];
  assign out_29[0] = out_29[1];
  assign out_32[0] = out_32[1];
  assign out_33[0] = out_33[1];
  assign out_34[0] = out_34[1];
  assign out_35[0] = out_35[1];
  assign out_38[0] = out_38[1];
  assign out_39[0] = out_39[1];
  assign out_40[0] = out_40[1];
  assign out_41[0] = out_41[1];
endmodule

module CodMatriz (
  input  C1,
  input  C2,
  input  C3,
  input  C4,
  input  C5,
  input  C6,
  input  F1,
  input  F2,
  input  F3,
  input  F4,
  input  F5,
  input  F6,
  output F1C1,
  output F1C2,
  output F1C3,
  output F1C4,
  output F1C5,
  output F1C6,
  output F2C1,
  output F2C2,
  output F2C3,
  output F2C4,
  output F2C5,
  output F2C6,
  output F3C1,
  output F3C2,
  output F3C3,
  output F3C4,
  output F3C5,
  output F3C6,
  output F4C1,
  output F4C2,
  output F4C3,
  output F4C4,
  output F4C5,
  output F4C6,
  output F5C1,
  output F5C2,
  output F5C3,
  output F5C4,
  output F5C5,
  output F5C6,
  output F6C1,
  output F6C2,
  output F6C3,
  output F6C4,
  output F6C5,
  output F6C6
);

  and and_1 (F1C1, F1, C1);
  and and_2 (F2C1, F2, C1);
  and and_3 (F3C1, F3, C1);
  and and_4 (F4C1, F4, C1);
  and and_5 (F5C1, F5, C1);
  and and_6 (F6C1, F6, C1);
  and and_7 (F1C2, F1, C2);
  and and_8 (F2C2, F2, C2);
  and and_9 (F3C2, F3, C2);
  and and_10 (F4C2, F4, C2);
  and and_11 (F5C2, F5, C2);
  and and_12 (F6C2, F6, C2);
  and and_13 (F1C3, F1, C3);
  and and_14 (F2C3, F2, C3);
  and and_15 (F3C3, F3, C3);
  and and_16 (F4C3, F4, C3);
  and and_17 (F5C3, F5, C3);
  and and_18 (F6C3, F6, C3);
  and and_19 (F1C4, F1, C4);
  and and_20 (F2C4, F2, C4);
  and and_21 (F3C4, F3, C4);
  and and_22 (F4C4, F4, C4);
  and and_23 (F5C4, F5, C4);
  and and_24 (F6C4, F6, C4);
  and and_25 (F1C5, F1, C5);
  and and_26 (F2C5, F2, C5);
  and and_27 (F3C5, F3, C5);
  and and_28 (F4C5, F4, C5);
  and and_29 (F5C5, F5, C5);
  and and_30 (F6C5, F6, C5);
  and and_31 (F1C6, F1, C6);
  and and_32 (F2C6, F2, C6);
  and and_33 (F3C6, F3, C6);
  and and_34 (F4C6, F4, C6);
  and and_35 (F5C6, F5, C6);
  and and_36 (F6C6, F6, C6);
endmodule

module Movimiento (
  input  Boton,
  input  M1,
  input  M0,
  output Ganoo,
  output S7,
  output S6,
  output S5,
  output S4,
  output S3,
  output S2,
  output S1,
  output S0,
  output check_pozo,
  output F2,
  output F1,
  output F0,
  output C2,
  output C1,
  output C0
);

  wire and_1_out, and_2_out, and_3_out, clock_1_out, control_1_columna, control_1_fila, d_ff_1_q, d_ff_2_q,
       d_ff_3_q, d_ff_4_q, hielo_1_out_8, not_1_out, not_2_out, or_1_out, submovimiento_1_restaracolumna,
       submovimiento_1_restarafila, submovimiento_1_sumaracolumna, submovimiento_1_sumarafila;

  or or_1 (or_1_out, hielo_1_out_8, Boton);
  and and_1 (and_1_out, ~Ganoo, ~check_pozo, or_1_out);  // AND_Gate
  D_Flip_Flop d_ff_1 (
    .D(submovimiento_1_sumarafila), .clk(submovimiento_1_sumarafila), .Q(d_ff_1_q),
    .reset(submovimiento_1_restarafila));  // open: Qn, preset
  SubMovimiento submovimiento_1 (
    .BotonMov(and_1_out), .M1(M1), .M0(M0), .SumarAFila(submovimiento_1_sumarafila),
    .RestarAFila(submovimiento_1_restarafila), .SumarAColumna(submovimiento_1_sumaracolumna),
    .RestarAColumna(submovimiento_1_restaracolumna));
  D_Flip_Flop d_ff_2 (
    .D(submovimiento_1_sumaracolumna), .clk(submovimiento_1_sumaracolumna), .Q(d_ff_2_q),
    .reset(submovimiento_1_restaracolumna));  // open: Qn, preset
  Control control_1 (.M1(M1), .M0(M0), .Fila(control_1_fila), .Columna(control_1_columna));
  D_Flip_Flop d_ff_3 (
    .D(submovimiento_1_restarafila), .clk(submovimiento_1_restarafila), .Q(d_ff_3_q),
    .reset(submovimiento_1_sumarafila));  // open: Qn, preset
  D_Flip_Flop d_ff_4 (
    .D(submovimiento_1_restaracolumna), .clk(submovimiento_1_restaracolumna), .Q(d_ff_4_q),
    .reset(submovimiento_1_sumaracolumna));  // open: Qn, preset
  and and_2 (and_2_out, and_1_out, control_1_fila);
  and and_3 (and_3_out, and_1_out, control_1_columna);
  not not_1 (not_1_out, and_3_out);
  not not_2 (not_2_out, and_2_out);
  Columna columna_1 (.Sumar(d_ff_2_q), .Restar(d_ff_4_q), .Ck(not_1_out), .C2(C2), .C1(C1), .C0(C0));
  Fila fila_1 (.Sumar(d_ff_1_q), .Restar(d_ff_3_q), .Ck(not_2_out), .F2(F2), .F1(F1), .F0(F0));
  Clock clock_1 (.out(clock_1_out));
  Hielo hielo_1 (.x2(C2), .x1(C1), .x0(C0), .y2(F2), .y1(F1), .y0(F0), .Reloj(clock_1_out), .out_8(hielo_1_out_8));
  Premio premio_1 (
    .x2(C2), .x1(C1), .x0(C0), .y2(F2), .y1(F1), .y0(F0), .check_pozo(check_pozo), .Ganoo(Ganoo), .S7(S7),
    .S6(S6), .S5(S5), .S4(S4), .S3(S3), .S2(S2), .S1(S1), .S0(S0));
  Pozo pozo_1 (.x2(C2), .x1(C1), .x0(C0), .y2(F2), .y1(F1), .y0(F0), .check_pozo(check_pozo));

  // Notes on the sheet:
  //   00 = Abajo(+Fila)
  //   10 = Arriba(-Fila)
  //   01 = Derecha(+Col)
  //   11 = Izquierda(-Col)
endmodule

module SubMovimiento (
  input  BotonMov,
  input  M1,
  input  M0,
  output SumarAFila,
  output RestarAFila,
  output SumarAColumna,
  output RestarAColumna
);

  and and_1 (SumarAFila, ~M1, BotonMov, ~M0);  // AND_Gate
  and and_2 (SumarAColumna, ~M1, BotonMov, M0);  // AND_Gate
  and and_3 (RestarAFila, M1, BotonMov, ~M0);  // AND_Gate
  and and_4 (RestarAColumna, M1, BotonMov, M0);
endmodule

module Fila (
  input  Sumar,
  input  Restar,
  input  Ck,
  output F2,
  output F1,
  output F0
);

  wire and_1_out, and_2_out, and_3_out, and_4_out, and_5_out, Fila0_out, Fila6_out, nand_1_out, or_1_out,
       or_2_out;

  and and_1 (and_1_out, and_4_out, ~F1);  // AND_Gate
  nand nand_1 (nand_1_out, Fila6_out, Sumar);
  and and_2 (and_2_out, and_5_out, F1);
  or or_1 (or_1_out, and_1_out, and_2_out);
  T_Flip_Flop t_ff_1 (.T(or_1_out), .clk(and_3_out), .Q(F2), .reset(Fila0_out));  // open: Qn, preset
  and and_3 (and_3_out, Ck, nand_1_out);
  and and_4 (and_4_out, Restar, ~F0);  // AND_Gate
  and and_5 (and_5_out, Sumar, F0);
  or or_2 (or_2_out, and_4_out, and_5_out);
  T_Flip_Flop t_ff_2 (.T(or_2_out), .clk(and_3_out), .Q(F1), .reset(Fila0_out));  // open: Qn, preset
  and Fila0 (Fila0_out, F2, F1, F0);
  T_Flip_Flop t_ff_3 (.T(1'b1), .clk(and_3_out), .Q(F0), .reset(Fila0_out));  // open: Qn, preset
  and Fila6 (Fila6_out, F2, ~F1, F0);  // AND_Gate
endmodule

module Columna (
  input  Sumar,
  input  Restar,
  input  Ck,
  output C2,
  output C1,
  output C0
);

  wire and_1_out, and_2_out, and_3_out, and_4_out, and_5_out, Fila0_out, Fila6_out, nand_1_out, or_1_out,
       or_2_out;

  and and_1 (and_1_out, and_4_out, ~C1);  // AND_Gate
  nand nand_1 (nand_1_out, Fila6_out, Sumar);
  and and_2 (and_2_out, and_5_out, C1);
  or or_1 (or_1_out, and_1_out, and_2_out);
  T_Flip_Flop t_ff_1 (.T(or_1_out), .clk(and_3_out), .Q(C2), .reset(Fila0_out));  // open: Qn, preset
  and and_3 (and_3_out, Ck, nand_1_out);
  and and_4 (and_4_out, Restar, ~C0);  // AND_Gate
  and and_5 (and_5_out, Sumar, C0);
  or or_2 (or_2_out, and_4_out, and_5_out);
  T_Flip_Flop t_ff_2 (.T(or_2_out), .clk(and_3_out), .Q(C1), .reset(Fila0_out));  // open: Qn, preset
  and Fila0 (Fila0_out, C2, C1, C0);
  T_Flip_Flop t_ff_3 (.T(1'b1), .clk(and_3_out), .Q(C0), .reset(Fila0_out));  // open: Qn, preset
  and Fila6 (Fila6_out, C2, ~C1, C0);  // AND_Gate
endmodule

module Segment7 (
  input  A,
  input  B,
  input  C,
  output S1,
  output S2,
  output S3,
  output S4,
  output S5,
  output S6,
  output S7
);

  wire and_1_out, and_2_out, and_3_out, and_4_out, and_5_out, and_6_out, and_7_out, and_8_out, and_10_out,
       and_11_out, and_12_out, and_13_out, and_14_out, and_15_out;

  and and_1 (and_1_out, ~A, B);  // AND_Gate
  and and_2 (and_2_out, A, ~B);  // AND_Gate
  and and_3 (and_3_out, ~B, C);  // AND_Gate
  and and_4 (and_4_out, A, ~B);  // AND_Gate
  and and_5 (and_5_out, ~A, B, C);  // AND_Gate
  and and_6 (and_6_out, A, ~B);  // AND_Gate
  and and_7 (and_7_out, ~B, C);  // AND_Gate
  and and_8 (and_8_out, ~A, B, ~C);  // AND_Gate
  and and_9 (S5, ~B, C);  // AND_Gate
  and and_10 (and_10_out, A, ~B);  // AND_Gate
  and and_11 (and_11_out, ~B, C);  // AND_Gate
  and and_12 (and_12_out, ~A, B, ~C);  // AND_Gate
  and and_13 (and_13_out, A, ~B);  // AND_Gate
  and and_14 (and_14_out, ~A, B);  // AND_Gate
  and and_15 (and_15_out, ~B, ~C);  // AND_Gate
  or or_1 (S1, and_1_out, and_2_out, and_3_out);
  or or_2 (S2, and_4_out, and_5_out);
  not not_1 (S4, A);
  or or_3 (S6, and_10_out, and_11_out, and_12_out);
  or or_4 (S7, and_13_out, and_14_out, and_15_out);
  or or_5 (S3, and_6_out, and_7_out, and_8_out);
endmodule

module Control (
  input  M1,
  input  M0,
  output Fila,
  output Columna
);

  wire and_1_out, and_2_out, and_3_out, and_4_out;

  and and_1 (and_1_out, ~M1, ~M0);  // AND_Gate
  and and_2 (and_2_out, M1, ~M0);  // AND_Gate
  and and_3 (and_3_out, ~M1, M0);  // AND_Gate
  and and_4 (and_4_out, M1, M0);
  or or_1 (Fila, and_1_out, and_2_out);
  or or_2 (Columna, and_3_out, and_4_out);
endmodule

module Premio (
  input  x2,
  input  x1,
  input  x0,
  input  y2,
  input  y1,
  input  y0,
  input  check_pozo,
  output Ganoo,
  output S7,
  output S6,
  output S5,
  output S4,
  output S3,
  output S2,
  output S1,
  output S0
);

  wire and_1_out, and_2_out, muxgano_1_s0, muxgano_1_s1, muxgano_1_s2, muxgano_1_s3, muxgano_1_s4,
       muxgano_1_s5, muxgano_1_s6, muxgano_1_s7, or_1_out, subpremios_1_premio1, subpremios_1_premio2,
       subpremios_1_premio3, subpremios_1_premio4, subpremios_1_premio5, subpremios_1_premio6,
       subpremios_1_premio7, subpremios_1_premio8;
  wire [3:0] t_ff_1_q;
  wire [5:0] multiplier_1_out;

  Gano gano_1 (.C2(x2), .C1(x1), .C0(x0), .Gana(Ganoo));
  SubPremios subpremios_1 (
    .x2(x2), .x1(x1), .x0(x0), .y2(y2), .y1(y1), .y0(y0), .Premio1(subpremios_1_premio1),
    .Premio2(subpremios_1_premio2), .Premio3(subpremios_1_premio3), .Premio4(subpremios_1_premio4),
    .Premio5(subpremios_1_premio5), .Premio6(subpremios_1_premio6), .Premio7(subpremios_1_premio7),
    .Premio8(subpremios_1_premio8));
  or or_1 (or_1_out, subpremios_1_premio1, subpremios_1_premio2, subpremios_1_premio3, subpremios_1_premio4, subpremios_1_premio5, subpremios_1_premio6, subpremios_1_premio7, subpremios_1_premio8);
  T_Flip_Flop t_ff_1 (.T(1'b1), .clk(or_1_out), .Q(t_ff_1_q[0]));  // open: Qn, reset, preset
  T_Flip_Flop t_ff_2 (.T(t_ff_1_q[0]), .clk(or_1_out), .Q(t_ff_1_q[1]));  // open: Qn, reset, preset
  and and_1 (and_1_out, t_ff_1_q[0], t_ff_1_q[1]);
  Multiplier #(.width(6)) multiplier_1 (
    .a({2'b00, t_ff_1_q}), .b(6'b000101), .out(multiplier_1_out));  // open: cin, cout
  Multiplexer multiplexer_1 (.in0(muxgano_1_s6), .in1(1'b0), .out(S6), .sel(check_pozo));
  Multiplexer multiplexer_2 (.in0(muxgano_1_s7), .in1(1'b0), .out(S7), .sel(check_pozo));
  T_Flip_Flop t_ff_3 (.T(and_1_out), .clk(or_1_out), .Q(t_ff_1_q[2]));  // open: Qn, reset, preset
  Multiplexer multiplexer_3 (.in0(muxgano_1_s5), .in1(1'b0), .out(S5), .sel(check_pozo));
  and and_2 (and_2_out, and_1_out, t_ff_1_q[2]);
  T_Flip_Flop t_ff_4 (.T(and_2_out), .clk(or_1_out), .Q(t_ff_1_q[3]));  // open: Qn, reset, preset
  MUXGano muxgano_1 (
    .He(Ganoo), .E5(multiplier_1_out[5]), .in_2(multiplier_1_out[4]), .in_3(multiplier_1_out[3]),
    .in_4(multiplier_1_out[2]), .in_5(multiplier_1_out[1]), .E0(multiplier_1_out[0]), .S7(muxgano_1_s7),
    .S6(muxgano_1_s6), .S5(muxgano_1_s5), .S4(muxgano_1_s4), .S3(muxgano_1_s3), .S2(muxgano_1_s2),
    .S1(muxgano_1_s1), .S0(muxgano_1_s0));
  Multiplexer multiplexer_4 (.in0(muxgano_1_s4), .in1(1'b0), .out(S4), .sel(check_pozo));
  Multiplexer multiplexer_5 (.in0(muxgano_1_s3), .in1(1'b0), .out(S3), .sel(check_pozo));
  Multiplexer multiplexer_6 (.in0(muxgano_1_s2), .in1(1'b0), .out(S2), .sel(check_pozo));
  Multiplexer multiplexer_7 (.in0(muxgano_1_s1), .in1(1'b0), .out(S1), .sel(check_pozo));
  Multiplexer multiplexer_8 (.in0(muxgano_1_s0), .in1(1'b1), .out(S0), .sel(check_pozo));

  // Notes on the sheet:
  //   multiplicador  de cada premio por 5
  //   contador de cantidad de veces que se paso por "premio"
  //   contador de puntos (parcial)
endmodule

module SubPremios (
  input  x2,
  input  x1,
  input  x0,
  input  y2,
  input  y1,
  input  y0,
  output Premio1,
  output Premio2,
  output Premio3,
  output Premio4,
  output Premio5,
  output Premio6,
  output Premio7,
  output Premio8
);

  wire and_1_out, and_2_out, and_3_out, and_4_out, and_5_out, and_6_out, and_7_out, and_8_out, and_9_out,
       and_10_out, and_11_out, and_12_out, and_13_out, and_14_out, and_15_out, and_16_out, d_ff_1_q,
       d_ff_2_q, d_ff_3_q, d_ff_4_q, d_ff_5_q, d_ff_6_q, d_ff_7_q, d_ff_8_q;

  and and_1 (and_1_out, ~x2, x1, x0);  // AND_Gate
  and and_2 (and_2_out, ~y2, y1, ~y0);  // AND_Gate
  and and_3 (and_3_out, ~x2, ~x1, x0);  // AND_Gate
  and and_4 (and_4_out, ~y2, ~y1, ~y0);  // AND_Gate
  and and_5 (and_5_out, ~x2, x1, ~x0);  // AND_Gate
  and and_6 (and_6_out, ~y2, ~y1, y0);  // AND_Gate
  and and_7 (and_7_out, x2, ~x1, x0);  // AND_Gate
  and and_8 (and_8_out, ~y2, ~y1, y0);  // AND_Gate
  and and_9 (and_9_out, ~x2, ~x1, ~x0);  // AND_Gate
  and and_10 (and_10_out, ~y2, y1, ~y0);  // AND_Gate
  and and_11 (and_11_out, ~x2, ~x1, x0);  // AND_Gate
  and and_12 (and_12_out, ~y2, y1, y0);  // AND_Gate
  and and_13 (and_13_out, x2, ~x1, ~x0);  // AND_Gate
  and and_14 (and_14_out, y2, ~y1, ~y0);  // AND_Gate
  and and_15 (and_15_out, ~x2, ~x1, x0);  // AND_Gate
  and and_16 (and_16_out, y2, ~y1, y0);  // AND_Gate
  and and_17 (Premio1, and_3_out, ~d_ff_1_q, and_4_out);  // AND_Gate
  and and_18 (Premio3, and_7_out, ~d_ff_4_q, and_8_out);  // AND_Gate
  and and_19 (Premio4, and_9_out, ~d_ff_5_q, and_10_out);  // AND_Gate
  and and_20 (Premio5, and_1_out, ~d_ff_6_q, and_2_out);  // AND_Gate
  and and_21 (Premio6, and_11_out, ~d_ff_7_q, and_12_out);  // AND_Gate
  and and_22 (Premio7, and_13_out, ~d_ff_8_q, and_14_out);  // AND_Gate
  and and_23 (Premio8, and_15_out, ~d_ff_2_q, and_16_out);  // AND_Gate
  D_Flip_Flop d_ff_1 (.D(Premio1), .clk(Premio1), .Q(d_ff_1_q));  // open: Qn, preset, reset
  and and_24 (Premio2, and_5_out, ~d_ff_3_q, and_6_out);  // AND_Gate
  D_Flip_Flop d_ff_2 (.D(Premio8), .clk(Premio8), .Q(d_ff_2_q));  // open: Qn, preset, reset
  D_Flip_Flop d_ff_3 (.D(Premio2), .clk(Premio2), .Q(d_ff_3_q));  // open: Qn, preset, reset
  D_Flip_Flop d_ff_4 (.D(Premio3), .clk(Premio3), .Q(d_ff_4_q));  // open: Qn, preset, reset
  D_Flip_Flop d_ff_5 (.D(Premio4), .clk(Premio4), .Q(d_ff_5_q));  // open: Qn, preset, reset
  D_Flip_Flop d_ff_6 (.D(Premio5), .clk(Premio5), .Q(d_ff_6_q));  // open: Qn, preset, reset
  D_Flip_Flop d_ff_7 (.D(Premio6), .clk(Premio6), .Q(d_ff_7_q));  // open: Qn, preset, reset
  D_Flip_Flop d_ff_8 (.D(Premio7), .clk(Premio7), .Q(d_ff_8_q));  // open: Qn, preset, reset

  // Notes on the sheet:
  //   Columna
  //   Fila
  //   (Columna; Fila)
endmodule

module Gano (
  input  C2,
  input  C1,
  input  C0,
  output Gana
);

  and Gano (Gana, C2, ~C1, C0);  // AND_Gate
endmodule

module MUXGano (
  input  E5,
  input  in_2,
  input  in_3,
  input  in_4,
  input  in_5,
  input  E0,
  input  He,
  output S7,
  output S6,
  output S5,
  output S4,
  output S3,
  output S2,
  output S1,
  output S0
);

  wire and_7_out, and_8_out, and_9_out, and_10_out, and_11_out, and_12_out;
  wire [5:0] and_6_out, multiplier_1_out;

  and and_1 (and_6_out[5], He, E5);
  and and_2 (and_6_out[4], He, in_2);
  and and_3 (and_6_out[3], He, in_3);
  and and_4 (and_6_out[2], He, in_4);
  and and_5 (and_6_out[1], He, in_5);
  and and_6 (and_6_out[0], He, E0);
  Multiplier multiplier_1 (.a({2'b00, and_6_out}), .b(8'h5), .out({S7, S6, multiplier_1_out}));  // open: cin, cout
  and and_7 (and_7_out, ~He, E5);  // AND_Gate
  and and_8 (and_8_out, ~He, in_2);  // AND_Gate
  and and_9 (and_9_out, ~He, in_3);  // AND_Gate
  or or_1 (S5, multiplier_1_out[5], and_7_out);
  and and_10 (and_10_out, ~He, in_4);  // AND_Gate
  and and_11 (and_11_out, ~He, in_5);  // AND_Gate
  or or_2 (S4, multiplier_1_out[4], and_8_out);
  and and_12 (and_12_out, ~He, E0);  // AND_Gate
  or or_3 (S3, multiplier_1_out[3], and_9_out);
  or or_4 (S2, multiplier_1_out[2], and_10_out);
  or or_5 (S1, multiplier_1_out[1], and_11_out);
  or or_6 (S0, and_12_out, multiplier_1_out[0]);
endmodule

module Pozo (
  input  x2,
  input  x1,
  input  x0,
  input  y2,
  input  y1,
  input  y0,
  output check_pozo
);

  wire subpozo_1_out_7, subpozo_1_out_8, subpozo_1_out_9, subpozo_1_out_10;

  SubPozo subpozo_1 (
    .F2(x2), .f1(x1), .f0(x0), .C2(y2), .C1(y1), .C0(y0), .out_7(subpozo_1_out_7), .out_8(subpozo_1_out_8),
    .out_9(subpozo_1_out_9), .out_10(subpozo_1_out_10));
  or or_1 (check_pozo, subpozo_1_out_7, subpozo_1_out_8, subpozo_1_out_9, subpozo_1_out_10);

  // Notes on the sheet:
  //   pozo 1 : 4;1
  //   pozo 2 : 5;4
  //   pozo 3 : 3;5
  //   pozo 4 : 1;6
endmodule

module SubPozo (
  input  F2,
  input  f1,
  input  f0,
  input  C2,
  input  C1,
  input  C0,
  output out_7,
  output out_8,
  output out_9,
  output out_10
);

  wire and_1_out, and_2_out, and_3_out, and_4_out, and_5_out, and_6_out, and_7_out, and_8_out;

  and and_1 (and_1_out, ~F2, f1, f0);  // AND_Gate
  and and_2 (and_2_out, ~C2, ~C1, ~C0);  // AND_Gate
  and and_3 (and_3_out, ~F2, ~f1, ~f0);  // AND_Gate
  and and_4 (and_4_out, C2, ~C1, C0);  // AND_Gate
  and and_5 (and_5_out, F2, ~f1, ~f0);  // AND_Gate
  and and_6 (and_6_out, ~C2, C1, C0);  // AND_Gate
  and and_7 (and_7_out, ~F2, f1, ~f0);  // AND_Gate
  and and_8 (and_8_out, C2, ~C1, ~C0);  // AND_Gate
  and and_9 (out_7, and_1_out, and_2_out);
  and and_10 (out_8, and_3_out, and_4_out);
  and and_11 (out_9, and_5_out, and_6_out);
  and and_12 (out_10, and_7_out, and_8_out);

  // Notes on the sheet:
  //   x
  //   y
endmodule

module Hielo (
  input  x2,
  input  x1,
  input  x0,
  input  y2,
  input  y1,
  input  y0,
  input  Reloj,
  output out_8
);

  wire and_1_out, and_2_out, and_3_out, and_4_out, and_5_out, and_6_out, d_ff_1_q, d_ff_2_q, or_1_out;

  and and_1 (and_1_out, ~x2, ~x1, x0, ~y2, ~y1, y0);  // AND_Gate
  and and_2 (and_2_out, ~x2, x1, ~x0, ~y2, ~y1, ~y0);  // AND_Gate
  and and_3 (and_3_out, ~x2, x1, ~x0, ~y2, y1, ~y0);  // AND_Gate
  and and_4 (and_4_out, ~x2, x1, x0, ~y2, y1, y0);  // AND_Gate
  and and_5 (and_5_out, ~x2, ~x1, x0, y2, ~y1, ~y0);  // AND_Gate
  and and_6 (and_6_out, ~x2, x1, x0, y2, ~y1, ~y0);  // AND_Gate
  or or_1 (or_1_out, and_1_out, and_2_out, and_3_out, and_4_out, and_5_out, and_6_out);
  D_Flip_Flop d_ff_1 (.D(or_1_out), .clk(Reloj), .Q(d_ff_1_q));  // open: Qn, preset, reset
  xor xor_1 (out_8, d_ff_1_q, d_ff_2_q);
  D_Flip_Flop d_ff_2 (.D(d_ff_1_q), .clk(Reloj), .Q(d_ff_2_q));  // open: Qn, preset, reset

  // Notes on the sheet:
  //   (1;1)
  //   (2;0)
  //   (2;2)
  //   (3;3)
  //   (1;4)
  //   (3;4)
endmodule
